// Logisim project 32位ALU.circ as structural Verilog: 1 circuit, main circuit main
module main (
  input  [31:0] in_1,
  input  [31:0] in_2,
  input  [3:0] in_3,
  output [31:0] out_4,
  output out_5,
  output out_6,
  output out_7,
  output [31:0] out_8
);

  wire adder_1_cout, and_2_out, and_3_out, and_4_out, and_5_out, or_2_out, or_3_out, subtractor_1_bout;
  wire [0:0] comparator_1_lt, comparator_2_lt;
  wire [1:0] subtractor_1_out, subtractor_1_out_2, subtractor_1_out_3;
  wire [26:0] shifter_2_out;
  wire [31:0] adder_1_out, and_1_out, divider_1_out, divider_1_rem, multiplier_1_cout, multiplier_1_out,
       nor_1_out, or_1_out, shifter_1_out, xor_1_out;
  wire [31:6] subtractor_1_out_4;
  wire [31:27] shifter_2_out_2;

  Multiplier #(.width(32)) multiplier_1 (
    .a(in_2), .b(in_1), .out(multiplier_1_out), .cout(multiplier_1_cout));  // open: cin
  Divider #(.width(32)) divider_1 (.a(in_1), .b(in_2), .out(divider_1_out), .rem(divider_1_rem));  // open: upper
  Adder #(.width(32)) adder_1 (.a(in_1), .b(in_2), .out(adder_1_out), .cout(adder_1_cout));  // open: cin
  Subtractor #(.width(32)) subtractor_1 (
    .a(in_1), .b(in_2), .out({subtractor_1_out_4, subtractor_1_out_3, subtractor_1_out_2, subtractor_1_out}),
    .bout(subtractor_1_bout));  // open: bin
  Comparator #(.width(32)) comparator_1 (.a(in_1), .b(in_2), .lt(comparator_1_lt[0]));  // open: gt, eq
  Comparator #(.width(32), .mode("unsigned")) comparator_2 (
    .a(in_1), .b(in_2), .eq(out_7), .lt(comparator_2_lt[0]));  // open: gt
  Shifter #(.width(32)) shifter_1 (.in(in_1), .\dist (in_2[4:0]), .out(shifter_1_out));
  Shifter #(.width(32), .shift("lr")) shifter_2 (.in(in_1), .\dist (in_2[4:0]), .out({shifter_2_out_2, shifter_2_out}));
  assign and_1_out = in_1 & in_2;  // AND_Gate and_1, 32 bits wide
  assign or_1_out = in_1 | in_2;  // OR_Gate or_1, 32 bits wide
  assign xor_1_out = in_1 ^ in_2;  // XOR_Gate xor_1, 32 bits wide
  assign nor_1_out = ~(in_1 | in_2);  // NOR_Gate nor_1, 32 bits wide
  Multiplexer #(.select(4), .width(32), .disabled(0), .enable("false")) multiplexer_1 (
    .in0(shifter_1_out), .in1({shifter_2_out_2, shifter_2_out}), .in2({{5{in_1[31]}}, shifter_2_out}),
    .in3(multiplier_1_out), .in4(divider_1_out), .in5(adder_1_out),
    .in6({subtractor_1_out_4, subtractor_1_out_3, subtractor_1_out_2, subtractor_1_out}), .in7(and_1_out),
    .in8(or_1_out), .in9(xor_1_out), .in10(nor_1_out), .in11({{31{1'b0}}, comparator_1_lt[0]}),
    .in12({{31{1'b0}}, comparator_2_lt[0]}), .out(out_4), .sel(in_3));  // open: in13, in14, in15
  Multiplexer #(.select(4), .width(32), .disabled(0), .enable("false")) multiplexer_2 (
    .in0({32{1'b0}}), .in1({32{1'b0}}), .in2({32{1'b0}}), .in3(multiplier_1_cout), .in4(divider_1_rem),
    .in5({32{1'b0}}), .in6({32{1'b0}}), .in7({32{1'b0}}), .in8({32{1'b0}}), .in9({32{1'b0}}),
    .in10({32{1'b0}}), .in11({32{1'b0}}), .in12({32{1'b0}}), .in13({32{1'b0}}), .in14({32{1'b0}}),
    .in15({32{1'b0}}), .out(out_8), .sel(in_3));
  and and_2 (and_2_out, adder_1_out[31], ~in_2[31], in_1[31]);  // AND_Gate
  and and_3 (and_3_out, ~in_2[31], adder_1_out[31], ~in_1[31]);  // AND_Gate
  Multiplexer #(.select(4), .disabled(0), .enable("false")) multiplexer_3 (
    .in0(1'b0), .in1(1'b0), .in2(1'b0), .in3(1'b0), .in4(1'b0), .in5(or_2_out), .in6(or_3_out), .in7(1'b0),
    .in8(1'b0), .in9(1'b0), .in10(1'b0), .in11(1'b0), .in12(1'b0), .in13(1'b0), .in14(1'b0), .in15(1'b0),
    .out(out_6), .sel(in_3));
  Multiplexer #(.select(4), .disabled(0), .enable("false")) multiplexer_4 (
    .in0(1'b0), .in1(1'b0), .in2(1'b0), .in3(1'b0), .in4(1'b0), .in5(adder_1_cout), .in6(subtractor_1_bout),
    .in7(1'b0), .in8(1'b0), .in9(1'b0), .in10(1'b0), .in11(1'b0), .in12(1'b0), .in13(1'b0), .in14(1'b0),
    .in15(1'b0), .out(out_5), .sel(in_3));
  or or_2 (or_2_out, and_2_out, and_3_out);
  and and_4 (and_4_out, in_1[31], ~in_2[31], ~subtractor_1_out_4[31]);  // AND_Gate
  and and_5 (and_5_out, ~in_1[31], subtractor_1_out_4[31], in_2[31]);  // AND_Gate
  or or_3 (or_3_out, and_4_out, and_5_out);

  // Other names for the same wires on the sheet: X[31:0] = in_1; ALUop[3:0] = in_3; equal = out_7; OF = out_6;
  //   result[31:0] = out_4; result2[31:0] = out_8; UOF = out_5; Y[31:0] = in_2
endmodule
