// Logisim project 32寄存器.circ as structural Verilog: 1 circuit, main circuit main
module main (
  input  [4:0] in_1,
  input  in_2,
  input  [4:0] in_3,
  input  in_4,
  input  [4:0] in_5,
  input  [31:0] in_6,
  output [31:0] out_7,
  output [31:0] out_8
);

  wire demultiplexer_1_out0, demultiplexer_1_out1, demultiplexer_1_out2, demultiplexer_1_out3,
       demultiplexer_1_out4, demultiplexer_1_out5, demultiplexer_1_out6, demultiplexer_1_out7,
       demultiplexer_1_out8, demultiplexer_1_out9, demultiplexer_1_out10, demultiplexer_1_out11,
       demultiplexer_1_out12, demultiplexer_1_out13, demultiplexer_1_out14, demultiplexer_1_out15,
       demultiplexer_1_out16, demultiplexer_1_out17, demultiplexer_1_out18, demultiplexer_1_out19,
       demultiplexer_1_out20, demultiplexer_1_out21, demultiplexer_1_out22, demultiplexer_1_out23,
       demultiplexer_1_out24, demultiplexer_1_out25, demultiplexer_1_out26, demultiplexer_1_out27,
       demultiplexer_1_out28, demultiplexer_1_out29, demultiplexer_1_out30, demultiplexer_1_out31;
  wire [31:0] m0, m1, m2, m3, m4, m5, m6, m7, m8, m9, m10, m11, m12, m13, m14, m15, m16, m17, m18, m19, m20,
       m21, m22, m23, m24, m25, m26, m27, m28, m29, m30, m31;

  Demultiplexer #(.select(5), .enable("false")) demultiplexer_1 (
    .out0(demultiplexer_1_out0), .out1(demultiplexer_1_out1), .out2(demultiplexer_1_out2),
    .out3(demultiplexer_1_out3), .out4(demultiplexer_1_out4), .out5(demultiplexer_1_out5),
    .out6(demultiplexer_1_out6), .out7(demultiplexer_1_out7), .out8(demultiplexer_1_out8),
    .out9(demultiplexer_1_out9), .out10(demultiplexer_1_out10), .out11(demultiplexer_1_out11),
    .out12(demultiplexer_1_out12), .out13(demultiplexer_1_out13), .out14(demultiplexer_1_out14),
    .out15(demultiplexer_1_out15), .out16(demultiplexer_1_out16), .out17(demultiplexer_1_out17),
    .out18(demultiplexer_1_out18), .out19(demultiplexer_1_out19), .out20(demultiplexer_1_out20),
    .out21(demultiplexer_1_out21), .out22(demultiplexer_1_out22), .out23(demultiplexer_1_out23),
    .out24(demultiplexer_1_out24), .out25(demultiplexer_1_out25), .out26(demultiplexer_1_out26),
    .out27(demultiplexer_1_out27), .out28(demultiplexer_1_out28), .out29(demultiplexer_1_out29),
    .out30(demultiplexer_1_out30), .out31(demultiplexer_1_out31), .in(in_2), .sel(in_5));
  Register #(.width(32)) register_1 (.D(in_6), .en(demultiplexer_1_out3), .Q(m3), .clk(in_4));  // open: clr
  Register #(.width(32)) register_2 (.D(in_6), .en(demultiplexer_1_out28), .Q(m28), .clk(in_4));  // open: clr
  Register #(.width(32)) register_3 (.D(in_6), .en(demultiplexer_1_out29), .Q(m29), .clk(in_4));  // open: clr
  Register #(.width(32)) register_4 (.D({32{1'b0}}), .en(demultiplexer_1_out0), .Q(m0), .clk(in_4));  // open: clr
  Register #(.width(32)) register_5 (.D(in_6), .en(demultiplexer_1_out1), .Q(m1), .clk(in_4));  // open: clr
  Register #(.width(32)) register_6 (.D(in_6), .en(demultiplexer_1_out2), .Q(m2), .clk(in_4));  // open: clr
  Register #(.width(32)) register_7 (.D(in_6), .en(demultiplexer_1_out6), .Q(m6), .clk(in_4));  // open: clr
  Register #(.width(32)) register_8 (.D(in_6), .en(demultiplexer_1_out7), .Q(m7), .clk(in_4));  // open: clr
  Register #(.width(32)) register_9 (.D(in_6), .en(demultiplexer_1_out24), .Q(m24), .clk(in_4));  // open: clr
  Register #(.width(32)) register_10 (.D(in_6), .en(demultiplexer_1_out30), .Q(m30), .clk(in_4));  // open: clr
  Register #(.width(32)) register_11 (.D(in_6), .en(demultiplexer_1_out31), .Q(m31), .clk(in_4));  // open: clr
  Register #(.width(32)) register_12 (.D(in_6), .en(demultiplexer_1_out4), .Q(m4), .clk(in_4));  // open: clr
  Register #(.width(32)) register_13 (.D(in_6), .en(demultiplexer_1_out5), .Q(m5), .clk(in_4));  // open: clr
  Register #(.width(32)) register_14 (.D(in_6), .en(demultiplexer_1_out25), .Q(m25), .clk(in_4));  // open: clr
  Register #(.width(32)) register_15 (.D(in_6), .en(demultiplexer_1_out26), .Q(m26), .clk(in_4));  // open: clr
  Register #(.width(32)) register_16 (.D(in_6), .en(demultiplexer_1_out27), .Q(m27), .clk(in_4));  // open: clr
  Register #(.width(32)) register_17 (.D(in_6), .en(demultiplexer_1_out11), .Q(m11), .clk(in_4));  // open: clr
  Register #(.width(32)) register_18 (.D(in_6), .en(demultiplexer_1_out20), .Q(m20), .clk(in_4));  // open: clr
  Register #(.width(32)) register_19 (.D(in_6), .en(demultiplexer_1_out8), .Q(m8), .clk(in_4));  // open: clr
  Register #(.width(32)) register_20 (.D(in_6), .en(demultiplexer_1_out9), .Q(m9), .clk(in_4));  // open: clr
  Register #(.width(32)) register_21 (.D(in_6), .en(demultiplexer_1_out10), .Q(m10), .clk(in_4));  // open: clr
  Register #(.width(32)) register_22 (.D(in_6), .en(demultiplexer_1_out21), .Q(m21), .clk(in_4));  // open: clr
  Register #(.width(32)) register_23 (.D(in_6), .en(demultiplexer_1_out22), .Q(m22), .clk(in_4));  // open: clr
  Register #(.width(32)) register_24 (.D(in_6), .en(demultiplexer_1_out23), .Q(m23), .clk(in_4));  // open: clr
  Register #(.width(32)) register_25 (.D(in_6), .en(demultiplexer_1_out15), .Q(m15), .clk(in_4));  // open: clr
  Register #(.width(32)) register_26 (.D(in_6), .en(demultiplexer_1_out16), .Q(m16), .clk(in_4));  // open: clr
  Multiplexer #(.select(5), .width(32), .enable("false")) multiplexer_1 (
    .in0(m0), .in1(m1), .in2(m2), .in3(m3), .in4(m4), .in5(m5), .in6(m6), .in7(m7), .in8(m8), .in9(m9),
    .in10(m10), .in11(m11), .in12(m12), .in13(m13), .in14(m14), .in15(m15), .in16(m16), .in17(m17),
    .in18(m18), .in19(m19), .in20(m20), .in21(m21), .in22(m22), .in23(m23), .in24(m24), .in25(m25),
    .in26(m26), .in27(m27), .in28(m28), .in29(m29), .in30(m30), .in31(m31), .out(out_7), .sel(in_1));
  Register #(.width(32)) register_27 (.D(in_6), .en(demultiplexer_1_out13), .Q(m13), .clk(in_4));  // open: clr
  Register #(.width(32)) register_28 (.D(in_6), .en(demultiplexer_1_out14), .Q(m14), .clk(in_4));  // open: clr
  Register #(.width(32)) register_29 (.D(in_6), .en(demultiplexer_1_out17), .Q(m17), .clk(in_4));  // open: clr
  Register #(.width(32)) register_30 (.D(in_6), .en(demultiplexer_1_out18), .Q(m18), .clk(in_4));  // open: clr
  Register #(.width(32)) register_31 (.D(in_6), .en(demultiplexer_1_out12), .Q(m12), .clk(in_4));  // open: clr
  Register #(.width(32)) register_32 (.D(in_6), .en(demultiplexer_1_out19), .Q(m19), .clk(in_4));  // open: clr
  Multiplexer #(.select(5), .width(32), .enable("false")) multiplexer_2 (
    .in0(m0), .in1(m1), .in2(m2), .in3(m3), .in4(m4), .in5(m5), .in6(m6), .in7(m7), .in8(m8), .in9(m9),
    .in10(m10), .in11(m11), .in12(m12), .in13(m13), .in14(m14), .in15(m15), .in16(m16), .in17(m17),
    .in18(m18), .in19(m19), .in20(m20), .in21(m21), .in22(m22), .in23(m23), .in24(m24), .in25(m25),
    .in26(m26), .in27(m27), .in28(m28), .in29(m29), .in30(m30), .in31(m31), .out(out_8), .sel(in_3));

  // Other names for the same wires on the sheet: CLK = in_4; Din[31:0] = in_6; R1_num[4:0] = in_1; R2_num[4:0] = in_3;
  //   RD1[31:0] = out_7; RD2[31:0] = out_8; W_num[4:0] = in_5; WE = in_2
endmodule
