// Logisim project 4位寄存器.circ as structural Verilog: 1 circuit, main circuit main
module main (
  input  [4:0] in_1,
  input  [4:0] in_2,
  input  [4:0] in_3,
  input  [31:0] in_4,
  input  in_5,
  input  in_6,
  output [31:0] out_7,
  output [31:0] out_8
);

  wire demultiplexer_1_out0, demultiplexer_1_out1, demultiplexer_1_out2, demultiplexer_1_out3;
  wire [31:0] register_1_q, register_2_q, register_3_q, register_4_q;

  Demultiplexer #(.select(2), .enable("false")) demultiplexer_1 (
    .out0(demultiplexer_1_out0), .out1(demultiplexer_1_out1), .out2(demultiplexer_1_out2),
    .out3(demultiplexer_1_out3), .in(in_5), .sel(in_3[1:0]));
  Register #(.width(32)) register_1 (.D(in_4), .en(demultiplexer_1_out3), .Q(register_1_q), .clk(in_6));  // open: clr
  Register #(.width(32)) register_2 (
    .D({32{1'b0}}), .en(demultiplexer_1_out0), .Q(register_2_q), .clk(in_6));  // open: clr
  Register #(.width(32)) register_3 (.D(in_4), .en(demultiplexer_1_out1), .Q(register_3_q), .clk(in_6));  // open: clr
  Register #(.width(32)) register_4 (.D(in_4), .en(demultiplexer_1_out2), .Q(register_4_q), .clk(in_6));  // open: clr
  Multiplexer #(.select(2), .width(32), .enable("false")) multiplexer_1 (
    .in0(register_2_q), .in1(register_3_q), .in2(register_4_q), .in3(register_1_q), .out(out_7),
    .sel(in_1[1:0]));
  Multiplexer #(.select(2), .width(32), .enable("false")) multiplexer_2 (
    .in0(register_2_q), .in1(register_3_q), .in2(register_4_q), .in3(register_1_q), .out(out_8),
    .sel(in_2[1:0]));

  // Other names for the same wires on the sheet: CLK = in_6; Din[31:0] = in_4; R1_num[1:0] = in_1[1:0];
  //   R2_num[1:0] = in_2[1:0]; W_num[1:0] = in_3[1:0]; RD1[31:0] = out_7; RD2[31:0] = out_8; WE = in_5
endmodule
