// Logisim project cache测试.circ as structural Verilog: 5 circuits, main circuit 块交换状态机
module \块交换状态机  (
  input  En,
  input  Clk,
  input  Miss,
  output Byte0_Ready,
  output Byte1_Ready,
  output Byte2_Ready,
  output Byte3_Ready,
  output Byte0_Ready_2
);

  wire and_1_out, and_2_out, and_3_out, and_4_out, and_5_out, and_6_out, and_7_out, Next_Q0, Next_Q1,
       Next_Q2, Next_Q3, not_1_out, not_2_out, not_3_out, not_4_out, not_5_out, not_6_out, not_7_out,
       not_8_out, not_9_out, not_10_out, not_11_out, not_12_out, not_13_out, or_1_out, or_2_out, Q0, Q1, Q2,
       Q3;

  not not_1 (not_1_out, Q3);
  not not_2 (not_2_out, Q3);
  not not_3 (not_3_out, Q2);
  not not_4 (not_4_out, Q3);
  not not_5 (not_5_out, Q1);
  not not_6 (not_6_out, Q3);
  not not_7 (not_7_out, Q0);
  not not_8 (not_8_out, Q3);
  not not_9 (not_9_out, Q0);
  D_Flip_Flop d_ff_1 (.clk(Clk), .D(Next_Q3), .Q(Q3), .en(En));  // open: Qn, preset, reset
  D_Flip_Flop d_ff_2 (.clk(Clk), .D(Next_Q2), .Q(Q2), .en(En));  // open: Qn, preset, reset
  D_Flip_Flop d_ff_3 (.clk(Clk), .D(Next_Q1), .Q(Q1), .en(En));  // open: Qn, preset, reset
  D_Flip_Flop d_ff_4 (.clk(Clk), .D(Next_Q0), .Q(Q0), .en(En));  // open: Qn, preset, reset
  and and_1 (and_1_out, not_1_out, Q2, Q1, Q0);
  and and_2 (and_2_out, not_2_out, not_3_out, Q1, Q0);
  not not_10 (not_10_out, Q3);
  and and_3 (and_3_out, not_10_out, Q2, not_11_out);
  not not_11 (not_11_out, Q1);
  not not_12 (not_12_out, Q3);
  and and_4 (and_4_out, not_12_out, Q2, not_13_out);
  not not_13 (not_13_out, Q0);
  and and_5 (and_5_out, not_4_out, not_5_out, Q0);
  and and_6 (and_6_out, not_6_out, Q1, not_7_out);
  and and_7 (and_7_out, not_8_out, not_9_out);
  or or_1 (or_1_out, and_2_out, and_3_out, and_4_out);
  or or_2 (or_2_out, and_5_out, and_6_out);
  Decoder #(.select(4), .disabled(0), .enable("false")) decoder_1 (
    .out1(Byte0_Ready), .out3(Byte1_Ready), .out5(Byte2_Ready), .out7(Byte3_Ready), .out8(Byte0_Ready_2),
    .sel({Q3, Q2, Q1, Q0}));  // open: out0, out2, out4, out6, out9, out10, out11, out12, out13, out14, out15
  and and_8 (Next_Q3, and_1_out, Miss);
  and and_9 (Next_Q2, or_1_out, Miss);
  and and_10 (Next_Q1, Miss, or_2_out);
  and and_11 (Next_Q0, Miss, and_7_out);
endmodule

module \Cache块交换  (
  input  [15:0] Addr,
  input  [7:0] ByteDataIn,
  input  Miss,
  input  Enable,
  input  CLK,
  output [15:0] ByteAddrOut,
  output [31:0] BlockDataIn,
  output BlkDataReady
);

  wire \块交换状态机_1_byte0_ready , \块交换状态机_1_byte1_ready , \块交换状态机_1_byte2_ready , \块交换状态机_1_byte3_ready ;
  wire [7:0] register_1_q, register_2_q, register_3_q, register_4_q;

  assign ByteAddrOut = \块交换状态机_1_byte0_ready  ? {Addr[15:2], 2'b00} : 16'bz;  // Controlled_Buffer controlled_buffer_1
  \块交换状态机  \u_块交换状态机_1  (
    .Clk(CLK), .Miss(Miss), .En(Enable), .Byte0_Ready(\块交换状态机_1_byte0_ready ),
    .Byte1_Ready(\块交换状态机_1_byte1_ready ), .Byte2_Ready(\块交换状态机_1_byte2_ready ),
    .Byte3_Ready(\块交换状态机_1_byte3_ready ), .Byte0_Ready_2(BlkDataReady));
  assign ByteAddrOut = \块交换状态机_1_byte1_ready  ? {Addr[15:2], 2'b01} : 16'bz;  // Controlled_Buffer controlled_buffer_2
  assign ByteAddrOut = \块交换状态机_1_byte2_ready  ? {Addr[15:2], 2'b10} : 16'bz;  // Controlled_Buffer controlled_buffer_3
  assign ByteAddrOut = \块交换状态机_1_byte3_ready  ? {Addr[15:2], 2'b11} : 16'bz;  // Controlled_Buffer controlled_buffer_4
  Register register_1 (.D(ByteDataIn), .en(\块交换状态机_1_byte0_ready ), .Q(register_1_q), .clk(CLK));  // open: clr
  Register register_2 (.D(ByteDataIn), .en(\块交换状态机_1_byte1_ready ), .Q(register_2_q), .clk(CLK));  // open: clr
  Register register_3 (.D(ByteDataIn), .en(\块交换状态机_1_byte2_ready ), .Q(register_3_q), .clk(CLK));  // open: clr
  Register register_4 (.D(ByteDataIn), .en(\块交换状态机_1_byte3_ready ), .Q(register_4_q), .clk(CLK));  // open: clr
  assign BlockDataIn = BlkDataReady ? {register_4_q, register_3_q, register_2_q, register_1_q} : 32'bz;  // Controlled_Buffer controlled_buffer_5

  // Notes on the sheet:
  //   数据缓存寄存器
endmodule

module \Cache自动测试  (
  input  in_1
);

  wire and_2_out, Clk, comparator_1_lt, comparator_2_eq, comparator_3_eq, controlled_buffer_1_out, EN, Error,
       Go, Hit, Miss, or_1_out, RDY, Runing;
  wire [3:0] _1, _2, _3;
  wire [7:0] Dataout, rom_2_data;
  wire [15:0] adder_1_out, bit_extender_3_out, \cache块交换_1_byteaddrout , counter_1_q, subtractor_1_out,
       Test_num, \实际命中 , \校验和 , \缺失次数 , \访问次数 ;
  wire [31:0] bit_extender_1_out, bit_extender_2_out, \cache块交换_1_blockdatain , divider_1_out, divider_2_out,
       multiplier_1_out, rom_1_data;
  wire [31:4] divider_2_rem, divider_3_out, divider_3_rem;

  Clock clock_1 (.out(Clk));
  // Probe on Test_num
  not not_1 (Hit, Miss);
  Counter #(.width(16), .max('hffff)) \u_计数器  (.count(EN), .Q(Test_num), .clk(Clk));  // open: load, D, carry, clr
  and and_1 (EN, Hit, Go);
  and and_2 (and_2_out, Miss, RDY, Runing);
  // Probe on \实际命中 
  // Probe on Test_num
  Counter #(.width(16), .max('hffff)) counter_1 (
    .count(and_2_out), .Q(counter_1_q), .clk(Clk));  // open: load, D, carry, clr
  Subtractor #(.width(16)) subtractor_1 (.a(\访问次数 ), .b(\缺失次数 ), .out(subtractor_1_out));  // open: bin, bout
  Comparator #(.width(16)) comparator_1 (.a(\访问次数 ), .b(\缺失次数 ), .lt(comparator_1_lt));  // open: gt, eq
  Comparator #(.width(16)) comparator_2 (.a(Test_num), .b(16'h100), .eq(comparator_2_eq));  // open: gt, lt
  not not_2 (Runing, comparator_2_eq);
  Register #(.width(16)) register_1 (.D(counter_1_q), .en(EN), .Q(\缺失次数 ), .clk(Clk));  // open: clr
  Multiplexer #(.width(16), .disabled(0), .enable("false")) multiplexer_1 (
    .in0(subtractor_1_out), .in1({16{1'b0}}), .out(\实际命中 ), .sel(comparator_1_lt));
  // Probe on \缺失次数 
  // Probe on \校验和 
  ROM #(.addrWidth(16), .dataWidth(32)) rom_1 (.addr(Test_num), .data(rom_1_data));  // open: sel
  Counter #(.width(16), .max('hffff)) counter_2 (.count(EN), .Q(\访问次数 ), .clk(Clk));  // open: load, D, carry, clr
  cache cache_1 (
    .in_1(rom_1_data), .in_2(\cache块交换_1_blockdatain ), .in_3(RDY), .in_4(Clk), .out_5(Miss));  // open: out_6
  assign bit_extender_1_out = {{16{1'b0}}, \实际命中 };  // Bit_Extender bit_extender_1
  // Probe on \访问次数 
  Multiplier #(.width(32)) multiplier_1 (
    .a(bit_extender_1_out), .b(32'h64), .out(multiplier_1_out));  // open: cin, cout
  assign bit_extender_2_out = {{16{1'b0}}, \访问次数 };  // Bit_Extender bit_extender_2
  assign bit_extender_3_out = {{8{1'b0}}, Dataout};  // Bit_Extender bit_extender_3
  Divider #(.width(32)) divider_1 (
    .a(multiplier_1_out), .b(bit_extender_2_out), .out(divider_1_out));  // open: upper, rem
  LED \u_读数据出错  (.in(Error));
  Pull_Resistor #(.pull(1)) pull_resistor_1 (.node(Miss));
  LED \u_缺失  (.in(Miss));
  Adder #(.width(16)) adder_1 (.a(\校验和 ), .b(bit_extender_3_out), .out(adder_1_out));  // open: cin, cout
  Hex_Digit_Display hex_digit_display_1 (.value(_3), .dp(1'b1));
  \Cache块交换  \cache块交换_1  (
    .Addr(rom_1_data[15:0]), .ByteDataIn(rom_2_data), .Miss(Miss), .Enable(Runing), .CLK(Clk),
    .ByteAddrOut(\cache块交换_1_byteaddrout ), .BlockDataIn(\cache块交换_1_blockdatain ), .BlkDataReady(RDY));
  Register #(.width(16)) \u_校验和  (.D(adder_1_out), .en(EN), .Q(\校验和 ), .clk(Clk));  // open: clr
  Divider #(.width(32)) divider_2 (
    .a(divider_1_out), .b(32'ha), .out(divider_2_out), .rem({divider_2_rem, _1}));  // open: upper
  Hex_Digit_Display hex_digit_display_2 (.value(_2));  // open: dp
  Hex_Digit_Display hex_digit_display_3 (.value(_1));  // open: dp
  Divider #(.width(32)) divider_3 (
    .a(divider_2_out), .b(32'ha), .out({divider_3_out, _3}), .rem({divider_3_rem, _2}));  // open: upper
  ROM #(.addrWidth(16)) rom_2 (.addr(\cache块交换_1_byteaddrout ), .data(rom_2_data));  // open: sel
  Comparator comparator_3 (.a(Test_num[7:0]), .b(Dataout), .eq(comparator_3_eq));  // open: gt, lt
  assign controlled_buffer_1_out = Hit ? comparator_3_eq : 1'bz;  // Controlled_Buffer controlled_buffer_1
  Pull_Resistor #(.pull(1)) pull_resistor_2 (.node(controlled_buffer_1_out));
  or or_1 (or_1_out, controlled_buffer_1_out, ~in_1);  // OR_Gate
  not not_3 (Error, or_1_out);
  and and_3 (Go, Runing, or_1_out);

  // Other names for the same wires on the sheet: 时钟周期数[15:0] = Test_num; 读错误暂停 = in_1

  // Notes on the sheet:
  //   Trace存储器
  //   电路功能：测试Cache模块， ctrl+k启动时钟后，会自动对cache模块进行读数据测试，并将数据逐一读出进行校验和计算
  //   Address
  //   contents of rom_1 (hex, n*v repeats v):
  //   0 1 2 3 8 9 a b 10 11 12 13 20 21 22 23 8 9 a b 4 5 6 7 24 25 26 27 4 5 6 7 0 1 2 3 8 9 a b 8 9 a b
  //   20 21 22 23 28 29 2a 2b 24 25 26 27 4 5 6 7 24 25 26 27 0 1 2 3 8 9 a b 20 21 22 23 20 21 22 23 30
  //   31 32 33 4 5 6 7 24 25 26 27 4 5 6 7 0 1 2 3 8 9 a b 20 21 22 23 20 21 22 23 28 29 2a 2b 4 5 6 7 24
  //   25 26 27 24 25 26 27 0 1 2 3 8 9 a b 8 9 a b 20 21 22 23 30 31 32 33 4 5 6 7 24 25 26 27 24 25 26 27
  //   0 1 2 3 0 1 2 3 8 9 a b 20 21 22 23 28 29 2a 2b 4 5 6 7 24 25 26 27 4 5 6 7 0 1 2 3 8 9 a b 0 1 2 3
  //   20 21 22 23 30 31 32 33 24 25 26 27 4 5 6 7 24 25 26 27 0 1 2 3 8 9 a b 20 21 22 23 20 21 22 23 28
  //   29 2a 2b 4 5 6 7 24 25 26 27 4 5 6 7
  //   CLK 
  //   如果设计了不同的映射方式，可以将该电路中cache模块替换为对应Cache模块即可!
  //   ctrl+r复位，  错误暂停模式位为1时，数据命中但读出数据不正确时会暂停系统
  //   miss
  //   blockDataIn
  //   默认trace是顺序访问，所以测试系统中判断读错误的逻辑是地址和数据相等，如果更换了trace，这个逻辑不正确
  //   参数统计区
  //   BlkDataReady
  //   命中率
  //   电路状态稳定后显示最终命中率
  //   二级存储器
  //   Cache模拟器
  //   contents of rom_2 (hex, n*v repeats v):
  //   0 1 2 3 4 5 6 7 8 9 a b c d e f 10 11 12 13 14 15 16 17 18 19 1a 1b 1c 1d 1e 1f 20 21 22 23 24 25 26
  //   27 28 29 2a 2b 2c 2d 2e 2f 30 31 32 33 34 35 36 37 38 39 3a 3b 3c 3d 3e 3f 40 41 42 43 44 45 46 47
  //   48 49 4a 4b 4c 4d 4e 4f 50 51 52 53 54 55 56 57 58 59 5a 5b 5c 5d 5e 5f 60 61 62 63 64 65 66 67 68
  //   69 6a 6b 6c 6d 6e 6f 70 71 72 73 74 75 76 77 78 79 7a 7b 7c 7d 7e 7f 80 81 82 83 84 85 86 87 88 89
  //   8a 8b 8c 8d 8e 8f 90 91 92 93 94 95 96 97 98 99 9a 9b 9c 9d 9e 9f a0 a1 a2 a3 a4 a5 a6 a7 a8 a9 aa
  //   ab ac ad ae af b0 b1 b2 b3 b4 b5 b6 b7 b8 b9 ba bb bc bd be bf c0 c1 c2 c3 c4 c5 c6 c7 c8 c9 ca cb
  //   cc cd ce cf d0 d1 d2 d3 d4 d5 d6 d7 d8 d9 da db dc dd de df e0 e1 e2 e3 e4 e5 e6 e7 e8 e9 ea eb ec
  //   ed ee ef f0 f1 f2 f3 f4 f5 f6 f7 f8 f9 fa fb fc fd fe ff 0 1 2 3 4 5 6 7 8 9 a b c d e f 10 11 12 13
  //   14 15 16 17 18 19 1a 1b 1c 1d 1e 1f 20 21 22 23 24 25 26 27 28 29 2a 2b 2c 2d 2e 2f 30 31 32 33 34
  //   35 36 37 38 39 3a 3b 3c 3d 3e 3f 40 41 42 43 44 45 46 47 48 49 4a 4b 4c 4d 4e 4f 50 51 52 53 54 55
  //   56 57 58 59 5a 5b 5c 5d 5e 5f 60 61 62 63 64 65 66 67 68 69 6a 6b 6c 6d 6e 6f 70 71 72 73 74 75 76
  //   77 78 79 7a 7b 7c 7d 7e 7f 80 81 82 83 84 85 86 87 88 89 8a 8b 8c 8d 8e 8f 90 91 92 93 94 95 96 97
  //   98 99 9a 9b 9c 9d 9e 9f a0 a1 a2 a3 a4 a5 a6 a7 a8 a9 aa ab ac ad ae af b0 b1 b2 b3 b4 b5 b6 b7 b8
  //   b9 ba bb bc bd be bf c0 c1 c2 c3 c4 c5 c6 c7 c8 c9 ca cb cc cd ce cf d0 d1 d2 d3 d4 d5 d6 d7 d8 d9
  //   da db dc dd de df e0 e1 e2 e3 e4 e5 e6 e7 e8 e9 ea eb ec ed ee ef f0 f1 f2 f3 f4 f5 f6 f7 f8 f9 fa
  //   fb fc fd fe ff 0 1 2 3 4 5 6 7 8 9 a b c d e f 10 11 12 13 14 15 16 17 18 19 1a 1b 1c 1d 1e 1f 20 21
  //   22 23 24 25 26 27 28 29 2a 2b 2c 2d 2e 2f 30 31 32 33 34 35 36 37 38 39 3a 3b 3c 3d 3e 3f 40 41 42
  //   43 44 45 46 47 48 49 4a 4b 4c 4d 4e 4f 50 51 52 53 54 55 56 57 58 59 5a 5b 5c 5d 5e 5f 60 61 62 63
  //   64 65 66 67 68 69 6a 6b 6c 6d 6e 6f 70 71 72 73 74 75 76 77 78 79 7a 7b 7c 7d 7e 7f 80 81 82 83 84
  //   85 86 87 88 89 8a 8b 8c 8d 8e 8f 90 91 92 93 94 95 96 97 98 99 9a 9b 9c 9d 9e 9f a0 a1 a2 a3 a4 a5
  //   a6 a7 a8 a9 aa ab ac ad ae af b0 b1 b2 b3 b4 b5 b6 b7 b8 b9 ba bb bc bd be bf c0 c1 c2 c3 c4 c5 c6
  //   c7 c8 c9 ca cb cc cd ce cf d0 d1 d2 d3 d4 d5 d6 d7 d8 d9 da db dc dd de df e0 e1 e2 e3 e4 e5 e6 e7
  //   e8 e9 ea eb ec ed ee ef f0 f1 f2 f3 f4 f5 f6 f7 f8 f9 fa fb fc fd fe ff 0 1 2 3 4 5 6 7 8 9 a b c d
  //   e f 10 11 12 13 14 15 16 17 18 19 1a 1b 1c 1d 1e 1f 20 21 22 23 24 25 26 27 28 29 2a 2b 2c 2d 2e 2f
  //   30 31 32 33 34 35 36 37 38 39 3a 3b 3c 3d 3e 3f 40 41 42 43 44 45 46 47 48 49 4a 4b 4c 4d 4e 4f 50
  //   51 52 53 54 55 56 57 58 59 5a 5b 5c 5d 5e 5f 60 61 62 63 64 65 66 67 68 69 6a 6b 6c 6d 6e 6f 70 71
  //   72 73 74 75 76 77 78 79 7a 7b 7c 7d 7e 7f 80 81 82 83 84 85 86 87 88 89 8a 8b 8c 8d 8e 8f 90 91 92
  //   93 94 95 96 97 98 99 9a 9b 9c 9d 9e 9f a0 a1 a2 a3 a4 a5 a6 a7 a8 a9 aa ab ac ad ae af b0 b1 b2 b3
  //   b4 b5 b6 b7 b8 b9 ba bb bc bd be bf c0 c1 c2 c3 c4 c5 c6 c7 c8 c9 ca cb cc cd ce cf d0 d1 d2 d3 d4
  //   d5 d6 d7 d8 d9 da db dc dd de df e0 e1 e2 e3 e4 e5 e6 e7 e8 e9 ea eb ec ed ee ef f0 f1 f2 f3 f4 f5
  //   f6 f7 f8 f9 fa fb fc fd fe ff 0 1 2 3 4 5 6 7 8 9 a b c d e f 10 11 12 13 14 15 16 17 18 19 1a 1b 1c
  //   1d 1e 1f 20 21 22 23 24 25 26 27 28 29 2a 2b 2c 2d 2e 2f 30 31 32 33 34 35 36 37 38 39 3a 3b 3c 3d
  //   3e 3f 40 41 42 43 44 45 46 47 48 49 4a 4b 4c 4d 4e 4f 50 51 52 53 54 55 56 57 58 59 5a 5b 5c 5d 5e
  //   5f 60 61 62 63 64 65 66 67 68 69 6a 6b 6c 6d 6e 6f 70 71 72 73 74 75 76 77 78 79 7a 7b 7c 7d 7e 7f
  //   80 81 82 83 84 85 86 87 88 89 8a 8b 8c 8d 8e 8f 90 91 92 93 94 95 96 97 98 99 9a 9b 9c 9d 9e 9f a0
  //   a1 a2 a3 a4 a5 a6 a7 a8 a9 aa ab ac ad ae af b0 b1 b2 b3 b4 b5 b6 b7 b8 b9 ba bb bc bd be bf c0 c1
  //   c2 c3 c4 c5 c6 c7 c8 c9 ca cb cc cd ce cf d0 d1 d2 d3 d4 d5 d6 d7 d8 d9 da db dc dd de df e0 e1 e2
  //   e3 e4 e5 e6 e7 e8 e9 ea eb ec ed ee ef f0 f1 f2 f3 f4 f5 f6 f7 f8 f9 fa fb fc fd fe ff
endmodule

module cache (
  input  [31:0] in_1,
  input  [31:0] in_2,
  input  in_3,
  input  in_4,
  output out_5,
  output [7:0] out_6
);

  wire and_1_out, and_2_out, and_3_out, and_4_out, and_5_out, and_6_out, and_7_out, and_8_out, and_9_out,
       and_10_out, and_11_out, and_12_out, and_13_out, and_14_out, and_15_out, and_16_out, and_17_out,
       comparator_1_eq, comparator_2_eq, comparator_3_eq, comparator_4_eq, comparator_5_eq, comparator_6_eq,
       comparator_7_eq, comparator_8_eq, comparator_9_eq, comparator_10_eq, comparator_11_eq,
       comparator_12_eq, comparator_13_eq, comparator_14_eq, comparator_15_eq, comparator_16_eq, not_1_out,
       V0, V0_q, V1, V1_q, V2, V2_q, V3, V3_q, V4_q, V5_q, V6_q, V7_q, V8_q, V9_q, V10_q, V11_q, V12_q,
       V13_q, V14_q, V15_q, w00, w01, w02, w03, w10, w11, w12, w13, w20, w21, w22, w23, w30, w31, w32, w33,
       write0, write1, write2, write3;
  wire [1:0] lru_1_out_4, lru_2_out_4, lru_3_out_4, lru_4_out_4, multiplexer_10_out, multiplexer_11_out,
       multiplexer_12_out, multiplexer_13_out, vnum;
  wire [27:0] register_1_q, register_2_q, register_3_q, register_4_q, register_5_q, register_6_q,
       register_7_q, register_8_q, register_9_q, register_10_q, register_11_q, register_12_q, register_13_q,
       register_14_q, register_15_q, register_16_q;
  wire [31:0] D0, D1, D2, D3, dataout_t, register_17_q, register_18_q, register_19_q, register_20_q,
       register_21_q, register_22_q, register_23_q, register_24_q, register_25_q, register_26_q,
       register_27_q, register_28_q, register_29_q, register_30_q, register_31_q, register_32_q;

  Register #(.width(1)) u_V0 (.D(1'b1), .en(w00), .Q(V0_q), .clk(in_4));  // open: clr
  Register #(.width(1)) u_V1 (.D(1'b1), .en(w01), .Q(V1_q), .clk(in_4));  // open: clr
  Register #(.width(1)) u_V2 (.D(1'b1), .en(w02), .Q(V2_q), .clk(in_4));  // open: clr
  Register #(.width(1)) u_V3 (.D(1'b1), .en(w03), .Q(V3_q), .clk(in_4));  // open: clr
  Register #(.width(1)) V4 (.D(1'b1), .en(w10), .Q(V4_q), .clk(in_4));  // open: clr
  Register #(.width(1)) V5 (.D(1'b1), .en(w11), .Q(V5_q), .clk(in_4));  // open: clr
  Register #(.width(1)) V6 (.D(1'b1), .en(w12), .Q(V6_q), .clk(in_4));  // open: clr
  Register #(.width(1)) V7 (.D(1'b1), .en(w13), .Q(V7_q), .clk(in_4));  // open: clr
  Register #(.width(1)) V8 (.D(1'b1), .en(w20), .Q(V8_q), .clk(in_4));  // open: clr
  Register #(.width(1)) V9 (.D(1'b1), .en(w21), .Q(V9_q), .clk(in_4));  // open: clr
  Register #(.width(1)) V10 (.D(1'b1), .en(w22), .Q(V10_q), .clk(in_4));  // open: clr
  Register #(.width(1)) V11 (.D(1'b1), .en(w23), .Q(V11_q), .clk(in_4));  // open: clr
  Register #(.width(1)) V12 (.D(1'b1), .en(w30), .Q(V12_q), .clk(in_4));  // open: clr
  Register #(.width(1)) V13 (.D(1'b1), .en(w31), .Q(V13_q), .clk(in_4));  // open: clr
  Register #(.width(1)) V14 (.D(1'b1), .en(w32), .Q(V14_q), .clk(in_4));  // open: clr
  Register #(.width(1)) V15 (.D(1'b1), .en(w33), .Q(V15_q), .clk(in_4));  // open: clr
  Register #(.width(28)) register_1 (.D(in_1[31:4]), .en(w20), .Q(register_1_q), .clk(in_4));  // open: clr
  Register #(.width(28)) register_2 (.D(in_1[31:4]), .en(w21), .Q(register_2_q), .clk(in_4));  // open: clr
  Register #(.width(28)) register_3 (.D(in_1[31:4]), .en(w22), .Q(register_3_q), .clk(in_4));  // open: clr
  Register #(.width(28)) register_4 (.D(in_1[31:4]), .en(w23), .Q(register_4_q), .clk(in_4));  // open: clr
  Register #(.width(28)) register_5 (.D(in_1[31:4]), .en(w30), .Q(register_5_q), .clk(in_4));  // open: clr
  Register #(.width(28)) register_6 (.D(in_1[31:4]), .en(w31), .Q(register_6_q), .clk(in_4));  // open: clr
  Register #(.width(28)) register_7 (.D(in_1[31:4]), .en(w32), .Q(register_7_q), .clk(in_4));  // open: clr
  Register #(.width(28)) register_8 (.D(in_1[31:4]), .en(w33), .Q(register_8_q), .clk(in_4));  // open: clr
  Register #(.width(28)) register_9 (.D(in_1[31:4]), .en(w00), .Q(register_9_q), .clk(in_4));  // open: clr
  Comparator #(.width(28)) comparator_1 (.a(register_9_q), .b(in_1[31:4]), .eq(comparator_1_eq));  // open: gt, lt
  Register #(.width(28)) register_10 (.D(in_1[31:4]), .en(w01), .Q(register_10_q), .clk(in_4));  // open: clr
  Comparator #(.width(28)) comparator_2 (.a(register_10_q), .b(in_1[31:4]), .eq(comparator_2_eq));  // open: gt, lt
  Register #(.width(28)) register_11 (.D(in_1[31:4]), .en(w02), .Q(register_11_q), .clk(in_4));  // open: clr
  Comparator #(.width(28)) comparator_3 (.a(register_11_q), .b(in_1[31:4]), .eq(comparator_3_eq));  // open: gt, lt
  Register #(.width(28)) register_12 (.D(in_1[31:4]), .en(w03), .Q(register_12_q), .clk(in_4));  // open: clr
  Comparator #(.width(28)) comparator_4 (.a(register_12_q), .b(in_1[31:4]), .eq(comparator_4_eq));  // open: gt, lt
  Register #(.width(28)) register_13 (.D(in_1[31:4]), .en(w10), .Q(register_13_q), .clk(in_4));  // open: clr
  Comparator #(.width(28)) comparator_5 (.a(register_13_q), .b(in_1[31:4]), .eq(comparator_5_eq));  // open: gt, lt
  Register #(.width(28)) register_14 (.D(in_1[31:4]), .en(w11), .Q(register_14_q), .clk(in_4));  // open: clr
  Comparator #(.width(28)) comparator_6 (.a(register_14_q), .b(in_1[31:4]), .eq(comparator_6_eq));  // open: gt, lt
  Register #(.width(28)) register_15 (.D(in_1[31:4]), .en(w12), .Q(register_15_q), .clk(in_4));  // open: clr
  Comparator #(.width(28)) comparator_7 (.a(register_15_q), .b(in_1[31:4]), .eq(comparator_7_eq));  // open: gt, lt
  Register #(.width(28)) register_16 (.D(in_1[31:4]), .en(w13), .Q(register_16_q), .clk(in_4));  // open: clr
  Comparator #(.width(28)) comparator_8 (.a(register_16_q), .b(in_1[31:4]), .eq(comparator_8_eq));  // open: gt, lt
  Comparator #(.width(28)) comparator_9 (.a(register_1_q), .b(in_1[31:4]), .eq(comparator_9_eq));  // open: gt, lt
  Comparator #(.width(28)) comparator_10 (.a(register_2_q), .b(in_1[31:4]), .eq(comparator_10_eq));  // open: gt, lt
  Comparator #(.width(28)) comparator_11 (.a(register_3_q), .b(in_1[31:4]), .eq(comparator_11_eq));  // open: gt, lt
  Comparator #(.width(28)) comparator_12 (.a(register_4_q), .b(in_1[31:4]), .eq(comparator_12_eq));  // open: gt, lt
  Comparator #(.width(28)) comparator_13 (.a(register_5_q), .b(in_1[31:4]), .eq(comparator_13_eq));  // open: gt, lt
  Comparator #(.width(28)) comparator_14 (.a(register_6_q), .b(in_1[31:4]), .eq(comparator_14_eq));  // open: gt, lt
  Comparator #(.width(28)) comparator_15 (.a(register_7_q), .b(in_1[31:4]), .eq(comparator_15_eq));  // open: gt, lt
  Comparator #(.width(28)) comparator_16 (.a(register_8_q), .b(in_1[31:4]), .eq(comparator_16_eq));  // open: gt, lt
  Decoder #(.select(2), .disabled(0)) decoder_1 (
    .out0(write0), .out1(write1), .out2(write2), .out3(write3), .sel(in_1[3:2]), .en(and_1_out));
  and and_1 (and_1_out, in_3, out_5);
  and and_2 (and_2_out, comparator_1_eq, V0_q);
  and and_3 (and_3_out, comparator_2_eq, V1_q);
  and and_4 (and_4_out, comparator_3_eq, V2_q);
  and and_5 (and_5_out, comparator_4_eq, V3_q);
  and and_6 (and_6_out, comparator_5_eq, V4_q);
  and and_7 (and_7_out, comparator_6_eq, V5_q);
  and and_8 (and_8_out, comparator_7_eq, V6_q);
  and and_9 (and_9_out, comparator_8_eq, V7_q);
  and and_10 (and_10_out, comparator_9_eq, V8_q);
  and and_11 (and_11_out, comparator_10_eq, V9_q);
  and and_12 (and_12_out, comparator_11_eq, V10_q);
  and and_13 (and_13_out, comparator_12_eq, V11_q);
  and and_14 (and_14_out, comparator_13_eq, V12_q);
  and and_15 (and_15_out, comparator_14_eq, V13_q);
  and and_16 (and_16_out, comparator_15_eq, V14_q);
  and and_17 (and_17_out, comparator_16_eq, V15_q);
  Multiplexer #(.select(2), .enable("false")) multiplexer_1 (
    .in0(and_2_out), .in1(and_3_out), .in2(and_4_out), .in3(and_5_out), .out(V0), .sel(in_1[3:2]));
  Multiplexer #(.select(2), .enable("false")) multiplexer_2 (
    .in0(and_6_out), .in1(and_7_out), .in2(and_8_out), .in3(and_9_out), .out(V1), .sel(in_1[3:2]));
  Multiplexer #(.select(2), .enable("false")) multiplexer_3 (
    .in0(and_10_out), .in1(and_11_out), .in2(and_12_out), .in3(and_13_out), .out(V2), .sel(in_1[3:2]));
  Multiplexer #(.select(2), .enable("false")) multiplexer_4 (
    .in0(and_14_out), .in1(and_15_out), .in2(and_16_out), .in3(and_17_out), .out(V3), .sel(in_1[3:2]));
  Multiplexer #(.select(2), .width(8)) multiplexer_5 (
    .in0(dataout_t[7:0]), .in1(dataout_t[15:8]), .in2(dataout_t[23:16]), .in3(dataout_t[31:24]), .out(out_6),
    .sel(in_1[1:0]), .en(not_1_out));
  not not_1 (not_1_out, out_5);
  Register #(.width(32)) register_17 (.D(in_2), .en(w00), .Q(register_17_q), .clk(in_4));  // open: clr
  Register #(.width(32)) register_18 (.D(in_2), .en(w01), .Q(register_18_q), .clk(in_4));  // open: clr
  Register #(.width(32)) register_19 (.D(in_2), .en(w02), .Q(register_19_q), .clk(in_4));  // open: clr
  Register #(.width(32)) register_20 (.D(in_2), .en(w03), .Q(register_20_q), .clk(in_4));  // open: clr
  Register #(.width(32)) register_21 (.D(in_2), .en(w10), .Q(register_21_q), .clk(in_4));  // open: clr
  Register #(.width(32)) register_22 (.D(in_2), .en(w11), .Q(register_22_q), .clk(in_4));  // open: clr
  Register #(.width(32)) register_23 (.D(in_2), .en(w12), .Q(register_23_q), .clk(in_4));  // open: clr
  Register #(.width(32)) register_24 (.D(in_2), .en(w13), .Q(register_24_q), .clk(in_4));  // open: clr
  Register #(.width(32)) register_25 (.D(in_2), .en(w20), .Q(register_25_q), .clk(in_4));  // open: clr
  Register #(.width(32)) register_26 (.D(in_2), .en(w21), .Q(register_26_q), .clk(in_4));  // open: clr
  Register #(.width(32)) register_27 (.D(in_2), .en(w22), .Q(register_27_q), .clk(in_4));  // open: clr
  Register #(.width(32)) register_28 (.D(in_2), .en(w23), .Q(register_28_q), .clk(in_4));  // open: clr
  Register #(.width(32)) register_29 (.D(in_2), .en(w30), .Q(register_29_q), .clk(in_4));  // open: clr
  Register #(.width(32)) register_30 (.D(in_2), .en(w31), .Q(register_30_q), .clk(in_4));  // open: clr
  Register #(.width(32)) register_31 (.D(in_2), .en(w32), .Q(register_31_q), .clk(in_4));  // open: clr
  Register #(.width(32)) register_32 (.D(in_2), .en(w33), .Q(register_32_q), .clk(in_4));  // open: clr
  Multiplexer #(.select(2), .width(32), .enable("false")) multiplexer_6 (
    .in0(register_17_q), .in1(register_18_q), .in2(register_19_q), .in3(register_20_q), .out(D0),
    .sel(in_1[3:2]));
  Multiplexer #(.select(2), .width(32), .enable("false")) multiplexer_7 (
    .in0(register_21_q), .in1(register_22_q), .in2(register_23_q), .in3(register_24_q), .out(D1),
    .sel(in_1[3:2]));
  Multiplexer #(.select(2), .width(32), .enable("false")) multiplexer_8 (
    .in0(register_25_q), .in1(register_26_q), .in2(register_27_q), .in3(register_28_q), .out(D2),
    .sel(in_1[3:2]));
  Multiplexer #(.select(2), .width(32), .enable("false")) multiplexer_9 (
    .in0(register_29_q), .in1(register_30_q), .in2(register_31_q), .in3(register_32_q), .out(D3),
    .sel(in_1[3:2]));
  nor nor_1 (out_5, V0, V1, V2, V3);
  Multiplexer #(.width(2), .enable("false")) multiplexer_10 (
    .in0(vnum), .in1(lru_3_out_4), .out(multiplexer_10_out), .sel(write2));
  Multiplexer #(.width(2), .enable("false")) multiplexer_11 (
    .in0(vnum), .in1(lru_4_out_4), .out(multiplexer_11_out), .sel(write3));
  Multiplexer #(.width(2), .enable("false")) multiplexer_12 (
    .in0(vnum), .in1(lru_1_out_4), .out(multiplexer_12_out), .sel(write0));
  lru lru_1 (.in_2(in_4), .out_4(lru_1_out_4), .in_3(multiplexer_12_out), .in_1(out_5));
  Multiplexer #(.width(2), .enable("false")) multiplexer_13 (
    .in0(vnum), .in1(lru_2_out_4), .out(multiplexer_13_out), .sel(write1));
  lru lru_2 (.in_2(in_4), .out_4(lru_2_out_4), .in_3(multiplexer_13_out), .in_1(out_5));
  Decoder #(.select(2), .disabled(0)) decoder_2 (
    .out0(w02), .out1(w12), .out2(w22), .out3(w32), .sel(lru_3_out_4), .en(write2));
  lru lru_3 (.in_2(in_4), .out_4(lru_3_out_4), .in_3(multiplexer_10_out), .in_1(out_5));
  Decoder #(.select(2), .disabled(0)) decoder_3 (
    .out0(w03), .out1(w13), .out2(w23), .out3(w33), .sel(lru_4_out_4), .en(write3));
  lru lru_4 (.in_2(in_4), .out_4(lru_4_out_4), .in_3(multiplexer_11_out), .in_1(out_5));
  Decoder #(.select(2), .disabled(0)) decoder_4 (
    .out0(w00), .out1(w10), .out2(w20), .out3(w30), .sel(lru_1_out_4), .en(write0));
  Decoder #(.select(2), .disabled(0)) decoder_5 (
    .out0(w01), .out1(w11), .out2(w21), .out3(w31), .sel(lru_2_out_4), .en(write1));
  Priority_Encoder #(.select(2)) priority_encoder_1 (
    .in0(V0), .in1(V1), .in2(V2), .in3(V3), .out(vnum), .en_in(1'b1));  // open: gs, en_out
  Multiplexer #(.select(2), .width(32), .enable("false")) multiplexer_14 (
    .in0(D0), .in1(D1), .in2(D2), .in3(D3), .out(dataout_t), .sel(vnum));

  // Other names for the same wires on the sheet: Blkready = in_3; CLK = in_4; data[31:0] = in_2; Dataout[7:0] = out_6;
  //   miss = out_5; offset[1:0] = in_1[1:0]; 字节地址[31:0] = in_1; index[1:0] = in_1[3:2]; tag[27:0] = in_1[31:4]
endmodule

module lru (
  input  in_1,
  input  in_2,
  input  [1:0] in_3,
  output [1:0] out_4
);

  wire c0, c1, c2, c3, CLK, comparator_5_gt, comparator_6_gt, comparator_7_gt, decoder_1_out0,
       decoder_1_out1, decoder_1_out2, decoder_1_out3, n0, n1, n2, n3;
  wire [3:0] adder_1_out, adder_2_out, adder_3_out, adder_4_out, counter_1_q, counter_2_q, counter_3_q,
       counter_4_q, multiplexer_1_out, multiplexer_2_out, num;

  Comparator #(.width(4)) comparator_1 (.a(num), .b(counter_3_q), .eq(n2));  // open: gt, lt
  Priority_Encoder #(.select(2)) priority_encoder_1 (
    .in0(n0), .in1(n1), .in2(n2), .in3(n3), .out(out_4), .en_in(1'b1));  // open: gs, en_out
  Comparator #(.width(4)) comparator_2 (.a(num), .b(counter_1_q), .eq(n0));  // open: gt, lt
  Adder #(.width(4)) adder_1 (.a(counter_1_q), .b(4'b0001), .out(adder_1_out));  // open: cin, cout
  Comparator #(.width(4)) comparator_3 (.a(num), .b(counter_2_q), .eq(n1));  // open: gt, lt
  Adder #(.width(4)) adder_2 (.a(counter_2_q), .b(4'b0001), .out(adder_2_out));  // open: cin, cout
  Adder #(.width(4)) adder_3 (.a(counter_3_q), .b(4'b0001), .out(adder_3_out));  // open: cin, cout
  Comparator #(.width(4)) comparator_4 (.a(num), .b(counter_4_q), .eq(n3));  // open: gt, lt
  Adder #(.width(4)) adder_4 (.a(counter_4_q), .b(4'b0001), .out(adder_4_out));  // open: cin, cout
  Counter #(.width(4), .max('hf), .ongoal("stay"), .trigger("falling")) counter_1 (
    .D(adder_1_out), .Q(counter_1_q), .clk(CLK), .clr(c0));  // open: load, count, carry
  Counter #(.width(4), .max('hf), .ongoal("stay"), .trigger("falling")) counter_2 (
    .D(adder_2_out), .Q(counter_2_q), .clk(CLK), .clr(c1));  // open: load, count, carry
  Counter #(.width(4), .max('hf), .ongoal("stay"), .trigger("falling")) counter_3 (
    .D(adder_3_out), .Q(counter_3_q), .clk(CLK), .clr(c2));  // open: load, count, carry
  Counter #(.width(4), .max('hf), .ongoal("stay"), .trigger("falling")) counter_4 (
    .D(adder_4_out), .Q(counter_4_q), .clk(CLK), .clr(c3));  // open: load, count, carry
  and and_1 (CLK, ~in_1, in_2);  // AND_Gate
  Comparator #(.width(4), .mode("unsigned")) comparator_5 (
    .a(counter_1_q), .b(counter_2_q), .gt(comparator_5_gt));  // open: eq, lt
  Multiplexer #(.width(4), .enable("false")) multiplexer_1 (
    .in0(counter_4_q), .in1(counter_3_q), .out(multiplexer_1_out), .sel(comparator_6_gt));
  Comparator #(.width(4), .mode("unsigned")) comparator_6 (
    .a(counter_3_q), .b(counter_4_q), .gt(comparator_6_gt));  // open: eq, lt
  Multiplexer #(.width(4), .enable("false")) multiplexer_2 (
    .in0(counter_2_q), .in1(counter_1_q), .out(multiplexer_2_out), .sel(comparator_5_gt));
  Comparator #(.width(4), .mode("unsigned")) comparator_7 (
    .a(multiplexer_2_out), .b(multiplexer_1_out), .gt(comparator_7_gt));  // open: eq, lt
  Decoder #(.select(2), .enable("false")) decoder_1 (
    .out0(decoder_1_out0), .out1(decoder_1_out1), .out2(decoder_1_out2), .out3(decoder_1_out3), .sel(in_3));
  Multiplexer #(.width(4), .enable("false")) multiplexer_3 (
    .in0(multiplexer_1_out), .in1(multiplexer_2_out), .out(num), .sel(comparator_7_gt));
  D_Flip_Flop d_ff_1 (.clk(CLK), .D(decoder_1_out0), .Q(c0));  // open: Qn, preset, en, reset
  D_Flip_Flop d_ff_2 (.clk(CLK), .D(decoder_1_out1), .Q(c1));  // open: Qn, preset, en, reset
  D_Flip_Flop d_ff_3 (.clk(CLK), .D(decoder_1_out2), .Q(c2));  // open: Qn, preset, en, reset
  D_Flip_Flop d_ff_4 (.clk(CLK), .D(decoder_1_out3), .Q(c3));  // open: Qn, preset, en, reset

  // Other names for the same wires on the sheet: CLKin = in_2; L[1:0] = out_4; miss = in_1; read[1:0] = in_3
endmodule
