// Logisim project 全加器.circ as structural Verilog: 2 circuits, main circuit main
module main (
  input  in_1,
  input  in_2,
  input  in_3,
  output out_4,
  output out_5
);

  wire and_1_out, and_2_out, and_3_out;

  xor xor_1 (out_4, in_1, in_3, in_2);
  and and_1 (and_1_out, in_3, in_2);
  and and_2 (and_2_out, in_3, in_1);
  and and_3 (and_3_out, in_2, in_1);
  or or_1 (out_5, and_1_out, and_2_out, and_3_out);
endmodule

module feng (
  input  in_1,
  input  [31:0] in_2,
  input  [31:0] in_3,
  output out_4,
  output [31:0] out_5
);

  wire main_2_out_5, main_3_out_5, main_4_out_5, main_5_out_5, main_6_out_5, main_7_out_5, main_8_out_5,
       main_9_out_5, main_10_out_5, main_11_out_5, main_12_out_5, main_13_out_5, main_14_out_5,
       main_15_out_5, main_16_out_5, main_17_out_5, main_18_out_5, main_19_out_5, main_20_out_5,
       main_21_out_5, main_22_out_5, main_23_out_5, main_24_out_5, main_25_out_5, main_26_out_5,
       main_27_out_5, main_28_out_5, main_29_out_5, main_30_out_5, main_31_out_5, main_32_out_5;

  main main_1 (.in_1(in_3[31]), .in_2(main_4_out_5), .in_3(in_2[31]), .out_4(out_5[31]), .out_5(out_4));
  main main_2 (.in_1(in_2[0]), .in_2(in_1), .in_3(in_3[0]), .out_4(out_5[0]), .out_5(main_2_out_5));
  main main_3 (.in_1(in_2[1]), .in_2(main_2_out_5), .in_3(in_3[1]), .out_4(out_5[1]), .out_5(main_3_out_5));
  main main_4 (.in_1(in_3[30]), .in_2(main_6_out_5), .in_3(in_2[30]), .out_4(out_5[30]), .out_5(main_4_out_5));
  main main_5 (.in_1(in_2[2]), .in_2(main_3_out_5), .in_3(in_3[2]), .out_4(out_5[2]), .out_5(main_5_out_5));
  main main_6 (.in_1(in_3[29]), .in_2(main_8_out_5), .in_3(in_2[29]), .out_4(out_5[29]), .out_5(main_6_out_5));
  main main_7 (.in_1(in_2[3]), .in_2(main_5_out_5), .in_3(in_3[3]), .out_4(out_5[3]), .out_5(main_7_out_5));
  main main_8 (.in_1(in_3[28]), .in_2(main_10_out_5), .in_3(in_2[28]), .out_4(out_5[28]), .out_5(main_8_out_5));
  main main_9 (.in_1(in_2[4]), .in_2(main_7_out_5), .in_3(in_3[4]), .out_4(out_5[4]), .out_5(main_9_out_5));
  main main_10 (.in_1(in_3[27]), .in_2(main_12_out_5), .in_3(in_2[27]), .out_4(out_5[27]), .out_5(main_10_out_5));
  main main_11 (.in_1(in_2[5]), .in_2(main_9_out_5), .in_3(in_3[5]), .out_4(out_5[5]), .out_5(main_11_out_5));
  main main_12 (.in_1(in_3[26]), .in_2(main_14_out_5), .in_3(in_2[26]), .out_4(out_5[26]), .out_5(main_12_out_5));
  main main_13 (.in_1(in_2[6]), .in_2(main_11_out_5), .in_3(in_3[6]), .out_4(out_5[6]), .out_5(main_13_out_5));
  main main_14 (.in_1(in_3[25]), .in_2(main_16_out_5), .in_3(in_2[25]), .out_4(out_5[25]), .out_5(main_14_out_5));
  main main_15 (.in_1(in_2[7]), .in_2(main_13_out_5), .in_3(in_3[7]), .out_4(out_5[7]), .out_5(main_15_out_5));
  main main_16 (.in_1(in_3[24]), .in_2(main_18_out_5), .in_3(in_2[24]), .out_4(out_5[24]), .out_5(main_16_out_5));
  main main_17 (.in_1(in_2[8]), .in_2(main_15_out_5), .in_3(in_3[8]), .out_4(out_5[8]), .out_5(main_17_out_5));
  main main_18 (.in_1(in_3[23]), .in_2(main_20_out_5), .in_3(in_2[23]), .out_4(out_5[23]), .out_5(main_18_out_5));
  main main_19 (.in_1(in_2[9]), .in_2(main_17_out_5), .in_3(in_3[9]), .out_4(out_5[9]), .out_5(main_19_out_5));
  main main_20 (.in_1(in_3[22]), .in_2(main_22_out_5), .in_3(in_2[22]), .out_4(out_5[22]), .out_5(main_20_out_5));
  main main_21 (.in_1(in_2[10]), .in_2(main_19_out_5), .in_3(in_3[10]), .out_4(out_5[10]), .out_5(main_21_out_5));
  main main_22 (.in_1(in_3[21]), .in_2(main_25_out_5), .in_3(in_2[21]), .out_4(out_5[21]), .out_5(main_22_out_5));
  main main_23 (.in_1(in_2[11]), .in_2(main_21_out_5), .in_3(in_3[11]), .out_4(out_5[11]), .out_5(main_23_out_5));
  main main_24 (.in_1(in_2[12]), .in_2(main_23_out_5), .in_3(in_3[12]), .out_4(out_5[12]), .out_5(main_24_out_5));
  main main_25 (.in_1(in_3[20]), .in_2(main_26_out_5), .in_3(in_2[20]), .out_4(out_5[20]), .out_5(main_25_out_5));
  main main_26 (.in_1(in_3[19]), .in_2(main_28_out_5), .in_3(in_2[19]), .out_4(out_5[19]), .out_5(main_26_out_5));
  main main_27 (.in_1(in_2[13]), .in_2(main_24_out_5), .in_3(in_3[13]), .out_4(out_5[13]), .out_5(main_27_out_5));
  main main_28 (.in_1(in_3[18]), .in_2(main_30_out_5), .in_3(in_2[18]), .out_4(out_5[18]), .out_5(main_28_out_5));
  main main_29 (.in_1(in_2[14]), .in_2(main_27_out_5), .in_3(in_3[14]), .out_4(out_5[14]), .out_5(main_29_out_5));
  main main_30 (.in_1(in_3[17]), .in_2(main_32_out_5), .in_3(in_2[17]), .out_4(out_5[17]), .out_5(main_30_out_5));
  main main_31 (.in_1(in_2[15]), .in_2(main_29_out_5), .in_3(in_3[15]), .out_4(out_5[15]), .out_5(main_31_out_5));
  main main_32 (.in_1(in_3[16]), .in_2(main_31_out_5), .in_3(in_2[16]), .out_4(out_5[16]), .out_5(main_32_out_5));

  // Other names for the same wires on the sheet: A[31:0] = in_2; a0 = in_2[0]; a1 = in_2[1]; a2 = in_2[2];
  //   a3 = in_2[3]; a4 = in_2[4]; a5 = in_2[5]; a6 = in_2[6]; a7 = in_2[7]; a8 = in_2[8]; a9 = in_2[9];
  //   a10 = in_2[10]; a11 = in_2[11]; a12 = in_2[12]; a13 = in_2[13]; a14 = in_2[14]; a15 = in_2[15]; a16 = in_2[16];
  //   a17 = in_2[17]; a18 = in_2[18]; a19 = in_2[19]; a20 = in_2[20]; a21 = in_2[21]; a22 = in_2[22]; a23 = in_2[23];
  //   a24 = in_2[24]; a25 = in_2[25]; a26 = in_2[26]; a27 = in_2[27]; a28 = in_2[28]; a29 = in_2[29]; a30 = in_2[30];
  //   a31 = in_2[31]; B[31:0] = in_3; b0 = in_3[0]; b1 = in_3[1]; b2 = in_3[2]; b3 = in_3[3]; b4 = in_3[4];
  //   b5 = in_3[5]; b6 = in_3[6]; b7 = in_3[7]; b8 = in_3[8]; b9 = in_3[9]; b10 = in_3[10]; b11 = in_3[11];
  //   b12 = in_3[12]; b13 = in_3[13]; b14 = in_3[14]; b15 = in_3[15]; b16 = in_3[16]; b17 = in_3[17]; b18 = in_3[18];
  //   b19 = in_3[19]; b20 = in_3[20]; b21 = in_3[21]; b22 = in_3[22]; b23 = in_3[23]; b24 = in_3[24]; b25 = in_3[25];
  //   b26 = in_3[26]; b27 = in_3[27]; b28 = in_3[28]; b29 = in_3[29]; b30 = in_3[30]; b31 = in_3[31]; Y[31:0] = out_5;
  //   y0 = out_5[0]; y1 = out_5[1]; y2 = out_5[2]; y3 = out_5[3]; y4 = out_5[4]; y5 = out_5[5]; y6 = out_5[6];
  //   y7 = out_5[7]; y8 = out_5[8]; y9 = out_5[9]; y10 = out_5[10]; y11 = out_5[11]; y12 = out_5[12]; y13 = out_5[13];
  //   y14 = out_5[14]; y15 = out_5[15]; y16 = out_5[16]; y17 = out_5[17]; y18 = out_5[18]; y19 = out_5[19];
  //   y20 = out_5[20]; y21 = out_5[21]; y22 = out_5[22]; y23 = out_5[23]; y24 = out_5[24]; y25 = out_5[25];
  //   y26 = out_5[26]; y27 = out_5[27]; y28 = out_5[28]; y29 = out_5[29]; y30 = out_5[30]; y31 = out_5[31]
endmodule
