// Logisim project 单周期.circ as structural Verilog: 4 circuits, main circuit 单周期
module main (
  input  [31:0] in_1,
  output [3:0] out_2,
  output out_3,
  output out_4,
  output out_5,
  output out_6,
  output out_7,
  output out_8,
  output out_9,
  output out_10,
  output out_11,
  output out_12,
  output out_13,
  output out_14
);

  wire ADD, ADDI, ADDIU, ADDU, AND, and_1_out, and_2_out, ANDI, comparator_1_eq, J, NOR, not_1_out, OR,
       or_3_out, ORI, SLL, SLT, SLTI, SLTU, SRA, SRL, SUB;

  or or_1 (out_11, J, out_14);
  Comparator #(.width(6)) comparator_1 (.a(in_1[31:26]), .b({6{1'b0}}), .eq(comparator_1_eq));  // open: gt, lt
  or or_2 (out_12, out_8, ADDI, ADDIU, SLTI, out_6);
  or or_3 (or_3_out, ORI, ADDI, out_6, ADDIU, SLTI, ANDI);
  and and_1 (and_1_out, in_1[5], comparator_1_eq);
  and and_2 (and_2_out, comparator_1_eq, ~in_1[5]);  // AND_Gate
  or or_4 (out_13, out_3, out_14, or_3_out);
  or or_5 (out_10, or_3_out, out_8);
  Decoder #(.select(5), .disabled(0)) decoder_1 (
    .out0(ADD), .out1(ADDU), .out2(SUB), .out4(AND), .out5(OR), .out7(NOR), .out10(SLT), .out11(SLTU),
    .sel(in_1[4:0]), .en(and_1_out));  // open: out3, out6, out8, out9, out12, out13, out14, out15, out16, out17, out18, out19, out20, out21, out22, out23, out24, out25, out26, out27, out28, out29, out30, out31
  Decoder #(.select(5), .disabled(0)) decoder_2 (
    .out0(SLL), .out2(SRL), .out3(SRA), .out8(out_9), .out12(out_5), .sel(in_1[4:0]), .en(and_2_out));  // open: out1, out4, out5, out6, out7, out9, out10, out11, out13, out14, out15, out16, out17, out18, out19, out20, out21, out22, out23, out24, out25, out26, out27, out28, out29, out30, out31
  or or_6 (out_3, ADD, ADDU, SUB, AND, OR, NOR, SLT, SLTU, SLL, SRL, SRA);
  Decoder #(.select(5), .disabled(0)) decoder_3 (
    .out3(out_6), .out11(out_8), .sel(in_1[30:26]), .en(in_1[31]));  // open: out0, out1, out2, out4, out5, out6, out7, out8, out9, out10, out12, out13, out14, out15, out16, out17, out18, out19, out20, out21, out22, out23, out24, out25, out26, out27, out28, out29, out30, out31
  not not_1 (not_1_out, in_1[31]);
  Decoder #(.select(5), .disabled(0)) decoder_4 (
    .out2(J), .out3(out_14), .out4(out_4), .out5(out_7), .out8(ADDI), .out9(ADDIU), .out10(SLTI),
    .out12(ANDI), .out13(ORI), .sel(in_1[30:26]), .en(not_1_out));  // open: out0, out1, out6, out7, out11, out14, out15, out16, out17, out18, out19, out20, out21, out22, out23, out24, out25, out26, out27, out28, out29, out30, out31
  or or_7 (out_2[1], SUB, AND, NOR, SLT, ANDI, SLTI, SRL);
  or or_8 (out_2[2], SUB, ADD, ADDU, AND, SLTU, ADDIU, ANDI, out_8, out_6, ADDI);
  or or_9 (out_2[0], ANDI, ADDIU, ADDI, out_6, AND, ADD, ADDU, SLT, SRA, out_8, SLTI);
  or or_10 (out_2[3], OR, NOR, SLT, SLTI, ORI, SLTU);

  // Other names for the same wires on the sheet: ALU_src = out_10; ALUop[3:0] = out_2; BEQ = out_4; BNE = out_7;
  //   func[5:0] = in_1[5:0]; func1[4:0] = in_1[4:0]; func2 = in_1[5]; op[5:0] = in_1[31:26]; op1[4:0] = in_1[30:26];
  //   op2 = in_1[31]; JAL = out_14; JMP = out_11; JR = out_9; LW = out_6; MemtoReg = out_6; RegDst = out_3;
  //   RegWrite = out_13; SignExt = out_12; MemWrite = out_8; SW = out_8; SYSCALL = out_5
endmodule

module \单周期  (
);

  wire alu_1_out_7, and_1_out, and_2_out, CLK, main_1_out_3, main_1_out_4, main_1_out_5, main_1_out_6,
       main_1_out_7, main_1_out_8, main_1_out_9, main_1_out_10, main_1_out_11, main_1_out_13, main_1_out_14,
       or_1_out, or_2_out, SIGNEXT;
  wire [3:0] main_1_out_2;
  wire [4:0] multiplexer_3_out, multiplexer_4_out, multiplexer_5_out, multiplexer_6_out;
  wire [31:0] adder_1_out, adder_2_out, alu_1_out_4, bit_extender_1_out, bit_extender_2_out, mips_probe_1_p1,
       multiplexer_1_out, multiplexer_2_out, multiplexer_7_out, multiplexer_8_out, multiplexer_9_out,
       multiplexer_10_out, PC_q, ram_1_data, shifter_1_out, \寄存器堆_1_out_7 , \寄存器堆_1_out_8 ;

  Multiplexer #(.width(32), .enable("false")) multiplexer_1 (
    .in0(multiplexer_9_out), .in1({mips_probe_1_p1[31:28], mips_probe_1_p1[25:0], 2'b00}),
    .out(multiplexer_1_out), .sel(or_1_out));
  Clock clock_1 (.out(CLK));
  Multiplexer #(.width(32), .enable("false")) multiplexer_2 (
    .in0(multiplexer_1_out), .in1(\寄存器堆_1_out_7 ), .out(multiplexer_2_out), .sel(main_1_out_9));
  Register #(.width(32)) PC (.D(multiplexer_2_out), .Q(PC_q), .clk(CLK));  // open: en, clr
  or or_1 (or_1_out, main_1_out_14, main_1_out_11);
  // Mips_Probe mips_probe_1: pin names not known; wires that end beside it: mips_probe_1_p1
  ROM #(.addrWidth(10), .dataWidth(32)) rom_1 (.addr(PC_q[11:2]), .data(mips_probe_1_p1));  // open: sel
  Adder #(.width(32)) adder_1 (.a(32'h4), .b(PC_q), .out(adder_1_out));  // open: cin, cout
  Multiplexer #(.width(5), .enable("false")) multiplexer_3 (
    .in0(mips_probe_1_p1[20:16]), .in1(5'b00100), .out(multiplexer_3_out), .sel(main_1_out_5));
  Multiplexer #(.width(5), .enable("false")) multiplexer_4 (
    .in0(mips_probe_1_p1[20:16]), .in1(mips_probe_1_p1[15:11]), .out(multiplexer_4_out), .sel(main_1_out_3));
  assign bit_extender_1_out = {{16{1'b0}}, mips_probe_1_p1[15:0]};  // Bit_Extender bit_extender_1
  assign bit_extender_2_out = {{16{mips_probe_1_p1[15]}}, mips_probe_1_p1[15:0]};  // Bit_Extender bit_extender_2
  Multiplexer #(.width(5), .enable("false")) multiplexer_5 (
    .in0(mips_probe_1_p1[25:21]), .in1(5'b00010), .out(multiplexer_5_out), .sel(main_1_out_5));
  Multiplexer #(.width(5), .enable("false")) multiplexer_6 (
    .in0(multiplexer_4_out), .in1({5{1'b1}}), .out(multiplexer_6_out), .sel(main_1_out_11));
  main main_1 (
    .in_1(mips_probe_1_p1), .out_2(main_1_out_2), .out_3(main_1_out_3), .out_4(main_1_out_4),
    .out_5(main_1_out_5), .out_6(main_1_out_6), .out_7(main_1_out_7), .out_8(main_1_out_8),
    .out_9(main_1_out_9), .out_10(main_1_out_10), .out_11(main_1_out_11), .out_12(SIGNEXT),
    .out_13(main_1_out_13), .out_14(main_1_out_14));
  \寄存器堆  \u_寄存器堆_1  (
    .in_1(multiplexer_5_out), .in_2(main_1_out_13), .in_3(multiplexer_3_out), .in_4(CLK),
    .in_5(multiplexer_6_out), .in_6(multiplexer_10_out), .out_7(\寄存器堆_1_out_7 ), .out_8(\寄存器堆_1_out_8 ));
  Multiplexer #(.width(32), .enable("false")) multiplexer_7 (
    .in0(bit_extender_1_out), .in1(bit_extender_2_out), .out(multiplexer_7_out), .sel(SIGNEXT));
  Multiplexer #(.width(32), .enable("false")) multiplexer_8 (
    .in0(\寄存器堆_1_out_8 ), .in1(multiplexer_7_out), .out(multiplexer_8_out), .sel(main_1_out_10));
  ALU alu_1 (
    .in_1(\寄存器堆_1_out_7 ), .out_4(alu_1_out_4), .out_7(alu_1_out_7), .in_2(multiplexer_8_out),
    .in_3(main_1_out_2));  // open: out_5, out_6, out_8
  Shifter #(.width(32)) shifter_1 (.in(multiplexer_7_out), .\dist (5'b00010), .out(shifter_1_out));
  and and_1 (and_1_out, main_1_out_4, alu_1_out_7);
  and and_2 (and_2_out, main_1_out_7, ~alu_1_out_7);  // AND_Gate
  Adder #(.width(32)) adder_2 (.a(shifter_1_out), .b(adder_1_out), .out(adder_2_out));  // open: cin, cout
  or or_2 (or_2_out, and_1_out, and_2_out);
  Multiplexer #(.width(32), .enable("false")) multiplexer_9 (
    .in0(adder_1_out), .in1(adder_2_out), .out(multiplexer_9_out), .sel(or_2_out));
  Multiplexer #(.width(32), .enable("false")) multiplexer_10 (
    .in0(alu_1_out_4), .in1(ram_1_data), .out(multiplexer_10_out), .sel(main_1_out_6));
  RAM #(.addrWidth(10), .dataWidth(32), .bus("separate")) ram_1 (
    .addr(alu_1_out_4[11:2]), .din(\寄存器堆_1_out_8 ), .data(ram_1_data), .str(main_1_out_8), .clk(CLK));  // open: sel, ld, clr

  // Notes on the sheet:
  //   contents of rom_1 (hex, n*v repeats v):
  //   2010ffff 20110000 ae300200 22100001 22310004 ae300200 22100001 22310004 ae300200 22100001 22310004
  //   ae300200 22100001 22310004 ae300200 22100001 22310004 ae300200 22100001 22310004 ae300200 22100001
  //   22310004 ae300200 8020 2011001c 8e130200 8e340200 274402a 11000002 ae330200 ae140200 2231fffc
  //   1611fff8 22100004 2011001c 1611fff5 2002000a c 947*0 123123 0 0 12312 4*0 123123 27*0 123 11111111
endmodule

module ALU (
  input  [31:0] in_1,
  input  [31:0] in_2,
  input  [3:0] in_3,
  output [31:0] out_4,
  output out_5,
  output out_6,
  output out_7,
  output [31:0] out_8
);

  wire adder_1_cout, and_2_out, and_3_out, and_4_out, and_5_out, or_2_out, or_3_out, subtractor_1_bout;
  wire [0:0] comparator_1_lt, comparator_2_lt;
  wire [1:0] subtractor_1_out, subtractor_1_out_2, subtractor_1_out_3;
  wire [26:0] shifter_2_out;
  wire [31:0] adder_1_out, and_1_out, divider_1_out, divider_1_rem, multiplier_1_cout, multiplier_1_out,
       nor_1_out, or_1_out, shifter_1_out, xor_1_out;
  wire [31:6] subtractor_1_out_4;
  wire [31:27] shifter_2_out_2;

  Multiplier #(.width(32)) multiplier_1 (
    .a(in_2), .b(in_1), .out(multiplier_1_out), .cout(multiplier_1_cout));  // open: cin
  Divider #(.width(32)) divider_1 (.a(in_1), .b(in_2), .out(divider_1_out), .rem(divider_1_rem));  // open: upper
  Adder #(.width(32)) adder_1 (.a(in_1), .b(in_2), .out(adder_1_out), .cout(adder_1_cout));  // open: cin
  Subtractor #(.width(32)) subtractor_1 (
    .a(in_1), .b(in_2), .out({subtractor_1_out_4, subtractor_1_out_3, subtractor_1_out_2, subtractor_1_out}),
    .bout(subtractor_1_bout));  // open: bin
  Comparator #(.width(32)) comparator_1 (.a(in_1), .b(in_2), .lt(comparator_1_lt[0]));  // open: gt, eq
  Comparator #(.width(32), .mode("unsigned")) comparator_2 (
    .a(in_1), .b(in_2), .eq(out_7), .lt(comparator_2_lt[0]));  // open: gt
  Shifter #(.width(32)) shifter_1 (.in(in_1), .\dist (in_2[4:0]), .out(shifter_1_out));
  Shifter #(.width(32), .shift("lr")) shifter_2 (.in(in_1), .\dist (in_2[4:0]), .out({shifter_2_out_2, shifter_2_out}));
  assign and_1_out = in_1 & in_2;  // AND_Gate and_1, 32 bits wide
  assign or_1_out = in_1 | in_2;  // OR_Gate or_1, 32 bits wide
  assign xor_1_out = in_1 ^ in_2;  // XOR_Gate xor_1, 32 bits wide
  assign nor_1_out = ~(in_1 | in_2);  // NOR_Gate nor_1, 32 bits wide
  Multiplexer #(.select(4), .width(32), .disabled(0), .enable("false")) multiplexer_1 (
    .in0(shifter_1_out), .in1({shifter_2_out_2, shifter_2_out}), .in2({{5{in_1[31]}}, shifter_2_out}),
    .in3(multiplier_1_out), .in4(divider_1_out), .in5(adder_1_out),
    .in6({subtractor_1_out_4, subtractor_1_out_3, subtractor_1_out_2, subtractor_1_out}), .in7(and_1_out),
    .in8(or_1_out), .in9(xor_1_out), .in10(nor_1_out), .in11({{31{1'b0}}, comparator_1_lt[0]}),
    .in12({{31{1'b0}}, comparator_2_lt[0]}), .out(out_4), .sel(in_3));  // open: in13, in14, in15
  Multiplexer #(.select(4), .width(32), .disabled(0), .enable("false")) multiplexer_2 (
    .in0({32{1'b0}}), .in1({32{1'b0}}), .in2({32{1'b0}}), .in3(multiplier_1_cout), .in4(divider_1_rem),
    .in5({32{1'b0}}), .in6({32{1'b0}}), .in7({32{1'b0}}), .in8({32{1'b0}}), .in9({32{1'b0}}),
    .in10({32{1'b0}}), .in11({32{1'b0}}), .in12({32{1'b0}}), .in13({32{1'b0}}), .in14({32{1'b0}}),
    .in15({32{1'b0}}), .out(out_8), .sel(in_3));
  and and_2 (and_2_out, adder_1_out[31], ~in_2[31], in_1[31]);  // AND_Gate
  and and_3 (and_3_out, ~in_2[31], adder_1_out[31], ~in_1[31]);  // AND_Gate
  Multiplexer #(.select(4), .disabled(0), .enable("false")) multiplexer_3 (
    .in0(1'b0), .in1(1'b0), .in2(1'b0), .in3(1'b0), .in4(1'b0), .in5(or_2_out), .in6(or_3_out), .in7(1'b0),
    .in8(1'b0), .in9(1'b0), .in10(1'b0), .in11(1'b0), .in12(1'b0), .in13(1'b0), .in14(1'b0), .in15(1'b0),
    .out(out_6), .sel(in_3));
  Multiplexer #(.select(4), .disabled(0), .enable("false")) multiplexer_4 (
    .in0(1'b0), .in1(1'b0), .in2(1'b0), .in3(1'b0), .in4(1'b0), .in5(adder_1_cout), .in6(subtractor_1_bout),
    .in7(1'b0), .in8(1'b0), .in9(1'b0), .in10(1'b0), .in11(1'b0), .in12(1'b0), .in13(1'b0), .in14(1'b0),
    .in15(1'b0), .out(out_5), .sel(in_3));
  or or_2 (or_2_out, and_2_out, and_3_out);
  and and_4 (and_4_out, in_1[31], ~in_2[31], ~subtractor_1_out_4[31]);  // AND_Gate
  and and_5 (and_5_out, ~in_1[31], subtractor_1_out_4[31], in_2[31]);  // AND_Gate
  or or_3 (or_3_out, and_4_out, and_5_out);

  // Other names for the same wires on the sheet: X[31:0] = in_1; ALUop[3:0] = in_3; equal = out_7; OF = out_6;
  //   result[31:0] = out_4; result2[31:0] = out_8; UOF = out_5; Y[31:0] = in_2
endmodule

module \寄存器堆  (
  input  [4:0] in_1,
  input  in_2,
  input  [4:0] in_3,
  input  in_4,
  input  [4:0] in_5,
  input  [31:0] in_6,
  output [31:0] out_7,
  output [31:0] out_8
);

  wire demultiplexer_1_out0, demultiplexer_1_out1, demultiplexer_1_out2, demultiplexer_1_out3,
       demultiplexer_1_out4, demultiplexer_1_out5, demultiplexer_1_out6, demultiplexer_1_out7,
       demultiplexer_1_out8, demultiplexer_1_out9, demultiplexer_1_out10, demultiplexer_1_out11,
       demultiplexer_1_out12, demultiplexer_1_out13, demultiplexer_1_out14, demultiplexer_1_out15,
       demultiplexer_1_out16, demultiplexer_1_out17, demultiplexer_1_out18, demultiplexer_1_out19,
       demultiplexer_1_out20, demultiplexer_1_out21, demultiplexer_1_out22, demultiplexer_1_out23,
       demultiplexer_1_out24, demultiplexer_1_out25, demultiplexer_1_out26, demultiplexer_1_out27,
       demultiplexer_1_out28, demultiplexer_1_out29, demultiplexer_1_out30, demultiplexer_1_out31;
  wire [31:0] m0, m1, m2, m3, m4, m5, m6, m7, m8, m9, m10, m11, m12, m13, m14, m15, m16, m17, m18, m19, m20,
       m21, m22, m23, m24, m25, m26, m27, m28, m29, m30, m31;

  Demultiplexer #(.select(5), .enable("false")) demultiplexer_1 (
    .out0(demultiplexer_1_out0), .out1(demultiplexer_1_out1), .out2(demultiplexer_1_out2),
    .out3(demultiplexer_1_out3), .out4(demultiplexer_1_out4), .out5(demultiplexer_1_out5),
    .out6(demultiplexer_1_out6), .out7(demultiplexer_1_out7), .out8(demultiplexer_1_out8),
    .out9(demultiplexer_1_out9), .out10(demultiplexer_1_out10), .out11(demultiplexer_1_out11),
    .out12(demultiplexer_1_out12), .out13(demultiplexer_1_out13), .out14(demultiplexer_1_out14),
    .out15(demultiplexer_1_out15), .out16(demultiplexer_1_out16), .out17(demultiplexer_1_out17),
    .out18(demultiplexer_1_out18), .out19(demultiplexer_1_out19), .out20(demultiplexer_1_out20),
    .out21(demultiplexer_1_out21), .out22(demultiplexer_1_out22), .out23(demultiplexer_1_out23),
    .out24(demultiplexer_1_out24), .out25(demultiplexer_1_out25), .out26(demultiplexer_1_out26),
    .out27(demultiplexer_1_out27), .out28(demultiplexer_1_out28), .out29(demultiplexer_1_out29),
    .out30(demultiplexer_1_out30), .out31(demultiplexer_1_out31), .in(in_2), .sel(in_5));
  Register #(.width(32)) register_1 (.D(in_6), .en(demultiplexer_1_out3), .Q(m3), .clk(in_4));  // open: clr
  Register #(.width(32)) register_2 (.D(in_6), .en(demultiplexer_1_out28), .Q(m28), .clk(in_4));  // open: clr
  Register #(.width(32)) register_3 (.D(in_6), .en(demultiplexer_1_out29), .Q(m29), .clk(in_4));  // open: clr
  Register #(.width(32)) register_4 (.D({32{1'b0}}), .en(demultiplexer_1_out0), .Q(m0), .clk(in_4));  // open: clr
  Register #(.width(32)) register_5 (.D(in_6), .en(demultiplexer_1_out1), .Q(m1), .clk(in_4));  // open: clr
  Register #(.width(32)) register_6 (.D(in_6), .en(demultiplexer_1_out2), .Q(m2), .clk(in_4));  // open: clr
  Register #(.width(32)) register_7 (.D(in_6), .en(demultiplexer_1_out6), .Q(m6), .clk(in_4));  // open: clr
  Register #(.width(32)) register_8 (.D(in_6), .en(demultiplexer_1_out7), .Q(m7), .clk(in_4));  // open: clr
  Register #(.width(32)) register_9 (.D(in_6), .en(demultiplexer_1_out24), .Q(m24), .clk(in_4));  // open: clr
  Register #(.width(32)) register_10 (.D(in_6), .en(demultiplexer_1_out30), .Q(m30), .clk(in_4));  // open: clr
  Register #(.width(32)) register_11 (.D(in_6), .en(demultiplexer_1_out31), .Q(m31), .clk(in_4));  // open: clr
  Register #(.width(32)) register_12 (.D(in_6), .en(demultiplexer_1_out4), .Q(m4), .clk(in_4));  // open: clr
  Register #(.width(32)) register_13 (.D(in_6), .en(demultiplexer_1_out5), .Q(m5), .clk(in_4));  // open: clr
  Register #(.width(32)) register_14 (.D(in_6), .en(demultiplexer_1_out25), .Q(m25), .clk(in_4));  // open: clr
  Register #(.width(32)) register_15 (.D(in_6), .en(demultiplexer_1_out26), .Q(m26), .clk(in_4));  // open: clr
  Register #(.width(32)) register_16 (.D(in_6), .en(demultiplexer_1_out27), .Q(m27), .clk(in_4));  // open: clr
  Register #(.width(32)) register_17 (.D(in_6), .en(demultiplexer_1_out11), .Q(m11), .clk(in_4));  // open: clr
  Register #(.width(32)) register_18 (.D(in_6), .en(demultiplexer_1_out20), .Q(m20), .clk(in_4));  // open: clr
  Register #(.width(32)) register_19 (.D(in_6), .en(demultiplexer_1_out8), .Q(m8), .clk(in_4));  // open: clr
  Register #(.width(32)) register_20 (.D(in_6), .en(demultiplexer_1_out9), .Q(m9), .clk(in_4));  // open: clr
  Register #(.width(32)) register_21 (.D(in_6), .en(demultiplexer_1_out10), .Q(m10), .clk(in_4));  // open: clr
  Register #(.width(32)) register_22 (.D(in_6), .en(demultiplexer_1_out21), .Q(m21), .clk(in_4));  // open: clr
  Register #(.width(32)) register_23 (.D(in_6), .en(demultiplexer_1_out22), .Q(m22), .clk(in_4));  // open: clr
  Register #(.width(32)) register_24 (.D(in_6), .en(demultiplexer_1_out23), .Q(m23), .clk(in_4));  // open: clr
  Register #(.width(32)) register_25 (.D(in_6), .en(demultiplexer_1_out15), .Q(m15), .clk(in_4));  // open: clr
  Register #(.width(32)) register_26 (.D(in_6), .en(demultiplexer_1_out16), .Q(m16), .clk(in_4));  // open: clr
  Multiplexer #(.select(5), .width(32), .enable("false")) multiplexer_1 (
    .in0(m0), .in1(m1), .in2(m2), .in3(m3), .in4(m4), .in5(m5), .in6(m6), .in7(m7), .in8(m8), .in9(m9),
    .in10(m10), .in11(m11), .in12(m12), .in13(m13), .in14(m14), .in15(m15), .in16(m16), .in17(m17),
    .in18(m18), .in19(m19), .in20(m20), .in21(m21), .in22(m22), .in23(m23), .in24(m24), .in25(m25),
    .in26(m26), .in27(m27), .in28(m28), .in29(m29), .in30(m30), .in31(m31), .out(out_7), .sel(in_1));
  Register #(.width(32)) register_27 (.D(in_6), .en(demultiplexer_1_out13), .Q(m13), .clk(in_4));  // open: clr
  Register #(.width(32)) register_28 (.D(in_6), .en(demultiplexer_1_out14), .Q(m14), .clk(in_4));  // open: clr
  Register #(.width(32)) register_29 (.D(in_6), .en(demultiplexer_1_out17), .Q(m17), .clk(in_4));  // open: clr
  Register #(.width(32)) register_30 (.D(in_6), .en(demultiplexer_1_out18), .Q(m18), .clk(in_4));  // open: clr
  Register #(.width(32)) register_31 (.D(in_6), .en(demultiplexer_1_out12), .Q(m12), .clk(in_4));  // open: clr
  Register #(.width(32)) register_32 (.D(in_6), .en(demultiplexer_1_out19), .Q(m19), .clk(in_4));  // open: clr
  Multiplexer #(.select(5), .width(32), .enable("false")) multiplexer_2 (
    .in0(m0), .in1(m1), .in2(m2), .in3(m3), .in4(m4), .in5(m5), .in6(m6), .in7(m7), .in8(m8), .in9(m9),
    .in10(m10), .in11(m11), .in12(m12), .in13(m13), .in14(m14), .in15(m15), .in16(m16), .in17(m17),
    .in18(m18), .in19(m19), .in20(m20), .in21(m21), .in22(m22), .in23(m23), .in24(m24), .in25(m25),
    .in26(m26), .in27(m27), .in28(m28), .in29(m29), .in30(m30), .in31(m31), .out(out_8), .sel(in_3));

  // Other names for the same wires on the sheet: CLK = in_4; Din[31:0] = in_6; R1_num[4:0] = in_1; R2_num[4:0] = in_3;
  //   RD1[31:0] = out_7; RD2[31:0] = out_8; W_num[4:0] = in_5; WE = in_2
endmodule
