// Logisim project 海明编码.circ as structural Verilog: 1 circuit, main circuit 无错误
module \无错误  (
  input  [15:0] in_1,
  output [21:0] out_2
);

  xor xor_1 (out_2[21], out_2[0], out_2[1], in_1[0], in_1[1], in_1[2], in_1[3], in_1[4], in_1[5], in_1[6], in_1[7], in_1[8], in_1[9], in_1[10], in_1[11], in_1[12], in_1[13], in_1[14], in_1[15], out_2[15], out_2[7], out_2[3]);
  xor xor_2 (out_2[15], in_1[11], in_1[12], in_1[13], in_1[14], in_1[15]);
  xor xor_3 (out_2[7], in_1[4], in_1[5], in_1[6], in_1[7], in_1[8], in_1[9], in_1[10]);
  xor xor_4 (out_2[3], in_1[1], in_1[2], in_1[3], in_1[7], in_1[8], in_1[9], in_1[10], in_1[14], in_1[15]);
  xor xor_5 (out_2[0], in_1[0], in_1[1], in_1[3], in_1[4], in_1[6], in_1[8], in_1[10], in_1[11], in_1[13], in_1[15]);
  xor xor_6 (out_2[1], in_1[0], in_1[2], in_1[3], in_1[5], in_1[6], in_1[9], in_1[10], in_1[12], in_1[13]);

  assign {out_2[20:16], out_2[14:8], out_2[6:4], out_2[2]} = in_1;

  // Other names for the same wires on the sheet: P1 = out_2[0];
  //   海明码[21:0] = {out_2[21], in_1[15:11], out_2[15], in_1[10:4], out_2[7], in_1[3:1], out_2[3], in_1[0], out_2[1:0]};
  //   P2 = out_2[1]; D1 = in_1[0]; P3 = out_2[3]; D2 = in_1[1]; D3 = in_1[2]; D4 = in_1[3]; P4 = out_2[7];
  //   D5 = in_1[4]; D6 = in_1[5]; D7 = in_1[6]; D8 = in_1[7]; D9 = in_1[8]; D10 = in_1[9]; D11 = in_1[10];
  //   P5 = out_2[15]; D12 = in_1[11]; D13 = in_1[12]; D14 = in_1[13]; D15 = in_1[14]; D16 = in_1[15]; P6 = out_2[21]

  // Notes on the sheet:
  //   原始数据
endmodule
