// Logisim project 海明编码解码.circ as structural Verilog: 1 circuit, main circuit 解码
module \解码  (
  input  [21:0] in_1,
  output [15:0] out_2,
  output out_3,
  output out_4,
  output out_5
);

  wire G1, G2, G3, G4, G5, G6, or_1_out, or_2_out;
  wire [15:0] decoder_1_out2;

  xor xor_1 (G5, in_1[15], in_1[16], in_1[17], in_1[18], in_1[19], in_1[20]);
  xor xor_2 (G4, in_1[7], in_1[8], in_1[9], in_1[10], in_1[11], in_1[12], in_1[13], in_1[14]);
  xor xor_3 (G3, in_1[4], in_1[5], in_1[6], in_1[11], in_1[12], in_1[13], in_1[14], in_1[19], in_1[20], in_1[3]);
  xor xor_4 (G1, in_1[2], in_1[4], in_1[6], in_1[8], in_1[10], in_1[0], in_1[12], in_1[14], in_1[16], in_1[18], in_1[20]);
  xor xor_5 (G2, in_1[1], in_1[2], in_1[5], in_1[6], in_1[9], in_1[10], in_1[13], in_1[14], in_1[17], in_1[18]);
  xor xor_6 (G6, in_1[12], in_1[0], in_1[1], in_1[2], in_1[4], in_1[5], in_1[6], in_1[8], in_1[9], in_1[10], in_1[11], in_1[13], in_1[14], in_1[16], in_1[17], in_1[18], in_1[19], in_1[20], in_1[15], in_1[7], in_1[3], in_1[21]);
  or or_1 (or_1_out, G1, G2, G3, G4, G5);
  or or_2 (or_2_out, G6, or_1_out);
  and and_1 (out_4, or_1_out, G6);
  and and_2 (out_5, or_1_out, ~G6);  // AND_Gate
  not not_1 (out_3, or_2_out);
  Decoder #(.select(5), .enable("false")) decoder_1 (
    .out2(decoder_1_out2[0]), .out4(decoder_1_out2[1]), .out5(decoder_1_out2[2]), .out6(decoder_1_out2[3]),
    .out8(decoder_1_out2[4]), .out9(decoder_1_out2[5]), .out10(decoder_1_out2[6]), .out11(decoder_1_out2[7]),
    .out12(decoder_1_out2[8]), .out13(decoder_1_out2[9]), .out14(decoder_1_out2[10]),
    .out16(decoder_1_out2[11]), .out17(decoder_1_out2[12]), .out18(decoder_1_out2[13]),
    .out19(decoder_1_out2[14]), .out20(decoder_1_out2[15]), .sel({G5, G4, G3, G2, G1}));  // open: out0, out1, out3, out7, out15, out21, out22, out23, out24, out25, out26, out27, out28, out29, out30, out31
  assign out_2 = decoder_1_out2 ^ {in_1[20:16], in_1[14:8], in_1[6:4], in_1[2]};  // XOR_Gate xor_7, 16 bits wide

  // Other names for the same wires on the sheet: D1 = in_1[2]; D2 = in_1[4]; D3 = in_1[5]; D4 = in_1[6]; D5 = in_1[8];
  //   D6 = in_1[9]; D7 = in_1[10]; D8 = in_1[11]; D9 = in_1[12]; D10 = in_1[13]; D11 = in_1[14]; D12 = in_1[16];
  //   D13 = in_1[17]; D14 = in_1[18]; D15 = in_1[19]; D16 = in_1[20]; P1 = in_1[0]; P2 = in_1[1]; P3 = in_1[3];
  //   P4 = in_1[7]; P5 = in_1[15]; P6 = in_1[21]; 一位错 = out_4; 两位错 = out_5; 无错误 = out_3; 纠错后数据[15:0] = out_2
endmodule
